// Logisim project DesignVorschlag1.2.circ as structural Verilog: 18 circuits, main circuit main
module main (
);

  wire and_1_out, and_2_out, Button_2_out, clock_1_out, ExecutePipelineStage_1_is_aluop_out,
       ExecutePipelineStage_1_is_extop_out, ExecutePipelineStage_1_is_ramop_out,
       ExecutePipelineStage_1_jmp_condintional_out, ExecutePipelineStage_1_jmp_out,
       ExecutePipelineStage_1_jmp_relative_out, ExecutePipelineStage_1_ram_read_out,
       ExecutePipelineStage_1_ram_src_out, ExecutePipelineStage_1_ram_write_out,
       ExecutePipelineStage_1_use_ma_out, ExecutePipelineStage_1_whb_out, ExecutePipelineStage_1_wlb_out,
       ExternalDeviceController_1_ext0_clk, ExternalDeviceController_1_ext1_clk, InstrExec, InstrLoad,
       InstructionDecoder_1_isaluop, InstructionDecoder_1_isextop, InstructionDecoder_1_isramop,
       InstructionDecoder_1_jmp, InstructionDecoder_1_jmp_condintional, InstructionDecoder_1_jmp_relative,
       InstructionDecoder_1_ram_read, InstructionDecoder_1_ram_src, InstructionDecoder_1_ram_write,
       InstructionDecoder_1_rf_whb, InstructionDecoder_1_rf_wlb, InstructionDecoder_1_use_ma, JMP_PC_In,
       or_1_out, PipeliningController_1_pc_clk, Reset, VGAController_1_clk_out,
       WriteBackPipelineStage_1_is_aluop_out, WriteBackPipelineStage_1_jmp_out,
       WriteBackPipelineStage_1_whb_out, WriteBackPipelineStage_1_wlb_out;
  wire [1:0] ExecutePipelineStage_1_din_sel_out, InstructionDecoder_1_din_sel,
       PipeliningController_1_instructionforwarding, PipeliningController_1_instructionforwarding_2;
  wire [2:0] ExecutePipelineStage_1_jmp_condition_out, InstructionDecoder_1_jmp_conditionalmode;
  wire [3:0] bit_extender_1_out, bit_extender_2_out, ExecutePipelineStage_1_writeaddress_out,
       InstructionDecoder_1_reg1, InstructionDecoder_1_reg2, InstructionDecoder_1_writereg,
       WriteBackPipelineStage_1_writeaddress_out;
  wire [4:4] PipeliningController_1_instructionforwarding_3;
  wire [7:0] VGAController_1_pixx, VGAController_1_pixy;
  wire [15:0] adder_1_out, ALU_1_alu_flags, ALU_1_alu_output, counter_1_q, ExecutePipelineStage_1_ma_out,
       ExternalDeviceController_1_ext0_d0, ExternalDeviceController_1_ext0_d1,
       ExternalDeviceController_1_ext1_d0, ExternalDeviceController_1_ext1_d1, im_modifier_1_union,
       Immediate, InstructionDecoder_1_immediate, JMP_PC_Addr, multiplexer_1_out, multiplexer_2_out,
       multiplexer_3_out, multiplexer_4_out, multiplexer_5_out, multiplexer_6_out, Operand1, Operand2,
       PipeliningController_1_queryinstruction, RAM_1_dout, RegFile_1_ma, RegFile_1_operand1,
       RegFile_1_operand2, ROM_1_data, WriteBackPipelineStage_1_flags_out,
       WriteBackPipelineStage_1_writedata_out;
  wire [23:0] VGAController_1_rgb;

  Clock clock_1 (.out(clock_1_out));
  Button ResetButton (.out(Reset));
  or or_1 (or_1_out, PipeliningController_1_pc_clk, and_1_out);
  and and_1 (and_1_out, InstrExec, JMP_PC_In);
  Counter #(.max('hffff), .width(16)) counter_1 (
    .clr(Reset), .load(JMP_PC_In), .clk(or_1_out), .D(JMP_PC_Addr), .Q(counter_1_q));  // open: up, count, carry
  ClockController ClockController_1 (.RawCLK(clock_1_out), .InstrLoad(InstrLoad), .InstrExec(InstrExec));
  ROM #(.addrWidth(16), .dataWidth(16)) ROM_1 (.addr(counter_1_q), .data(ROM_1_data));
  PipeliningController PipeliningController_1 (
    .InstrLoad(InstrLoad), .InstrExec(InstrExec), .Reset(Reset), .InstructionIn(ROM_1_data),
    .ResolveStall(WriteBackPipelineStage_1_jmp_out), .PC_CLK(PipeliningController_1_pc_clk),
    .InstructionForwarding({PipeliningController_1_instructionforwarding_3[4], PipeliningController_1_instructionforwarding_2, PipeliningController_1_instructionforwarding}),
    .QueryInstruction(PipeliningController_1_queryinstruction));
  Hex_Digit_Display Hex_Digit_Display_1 (.value(PipeliningController_1_queryinstruction[15:12]));  // open: dp
  InstructionDecoder InstructionDecoder_1 (
    .Instruction(PipeliningController_1_queryinstruction), .Reg1(InstructionDecoder_1_reg1),
    .Reg2(InstructionDecoder_1_reg2), .WriteReg(InstructionDecoder_1_writereg),
    .Immediate(InstructionDecoder_1_immediate), .RF_WHB(InstructionDecoder_1_rf_whb),
    .RF_WLB(InstructionDecoder_1_rf_wlb), .DIn_Sel(InstructionDecoder_1_din_sel),
    .RAM_Src(InstructionDecoder_1_ram_src), .RAM_Read(InstructionDecoder_1_ram_read),
    .RAM_Write(InstructionDecoder_1_ram_write), .USE_MA(InstructionDecoder_1_use_ma),
    .JMP(InstructionDecoder_1_jmp), .JMP_Condintional(InstructionDecoder_1_jmp_condintional),
    .JMP_Relative(InstructionDecoder_1_jmp_relative),
    .JMP_ConditionalMode(InstructionDecoder_1_jmp_conditionalmode), .IsALUOP(InstructionDecoder_1_isaluop),
    .IsRAMOP(InstructionDecoder_1_isramop), .IsEXTOP(InstructionDecoder_1_isextop));  // open: Reg1Read, Reg2Read
  RegFile RegFile_1 (
    .WriteData(WriteBackPipelineStage_1_writedata_out), .WHB(WriteBackPipelineStage_1_whb_out),
    .WLB(WriteBackPipelineStage_1_wlb_out), .CLK(InstrExec), .ReadAddress1(InstructionDecoder_1_reg1),
    .ReadAddress2(InstructionDecoder_1_reg2), .WriteAddress(WriteBackPipelineStage_1_writeaddress_out),
    .Flags(WriteBackPipelineStage_1_flags_out), .IsALUOP(WriteBackPipelineStage_1_is_aluop_out),
    .Operand1(RegFile_1_operand1), .Operand2(RegFile_1_operand2), .MA(RegFile_1_ma));
  Multiplexer #(.select(2), .width(16)) multiplexer_1 (
    .in0(RegFile_1_operand1), .in1(RegFile_1_operand1), .in2(multiplexer_6_out), .in3(ALU_1_alu_flags),
    .out(multiplexer_1_out), .sel(PipeliningController_1_instructionforwarding));
  Multiplexer #(.select(2), .width(16)) multiplexer_2 (
    .in0(RegFile_1_operand2), .in1(RegFile_1_operand2), .in2(multiplexer_6_out), .in3(ALU_1_alu_flags),
    .out(multiplexer_2_out), .sel(PipeliningController_1_instructionforwarding_2));
  Multiplexer #(.width(16)) multiplexer_3 (
    .in0(RegFile_1_ma), .in1(multiplexer_6_out), .out(multiplexer_3_out),
    .sel(PipeliningController_1_instructionforwarding_3[4]));
  ExecutePipelineStage ExecutePipelineStage_1 (
    .InstrLoad(InstrLoad), .Reset(Reset), .Operand1(multiplexer_1_out), .Operand2(multiplexer_2_out),
    .Immediate(InstructionDecoder_1_immediate), .MA(multiplexer_3_out),
    .WriteAddress(InstructionDecoder_1_writereg), .WHB(InstructionDecoder_1_rf_whb),
    .WLB(InstructionDecoder_1_rf_wlb), .DIn_SEL(InstructionDecoder_1_din_sel),
    .RAM_Src(InstructionDecoder_1_ram_src), .RAM_Read(InstructionDecoder_1_ram_read),
    .RAM_Write(InstructionDecoder_1_ram_write), .Use_MA(InstructionDecoder_1_use_ma),
    .JMP(InstructionDecoder_1_jmp), .JMP_Conditional(InstructionDecoder_1_jmp_condintional),
    .JMP_Relative(InstructionDecoder_1_jmp_relative),
    .JMP_Condition(InstructionDecoder_1_jmp_conditionalmode), .Is_ALUOP(InstructionDecoder_1_isaluop),
    .Is_RAMOP(InstructionDecoder_1_isramop), .Is_EXTOP(InstructionDecoder_1_isextop),
    .Operand1_out(Operand1), .Operand2_out(Operand2), .Immediate_out(Immediate),
    .MA_out(ExecutePipelineStage_1_ma_out), .WriteAddress_out(ExecutePipelineStage_1_writeaddress_out),
    .WHB_out(ExecutePipelineStage_1_whb_out), .WLB_out(ExecutePipelineStage_1_wlb_out),
    .DIn_SEL_out(ExecutePipelineStage_1_din_sel_out), .RAM_Src_out(ExecutePipelineStage_1_ram_src_out),
    .RAM_Read_out(ExecutePipelineStage_1_ram_read_out), .RAM_Write_out(ExecutePipelineStage_1_ram_write_out),
    .Use_MA_out(ExecutePipelineStage_1_use_ma_out), .JMP_out(ExecutePipelineStage_1_jmp_out),
    .JMP_Condintional_out(ExecutePipelineStage_1_jmp_condintional_out),
    .JMP_Relative_out(ExecutePipelineStage_1_jmp_relative_out),
    .JMP_Condition_out(ExecutePipelineStage_1_jmp_condition_out),
    .IS_ALUOP_out(ExecutePipelineStage_1_is_aluop_out), .Is_RAMOP_out(ExecutePipelineStage_1_is_ramop_out),
    .Is_EXTOP_out(ExecutePipelineStage_1_is_extop_out));
  Multiplexer #(.width(16)) multiplexer_4 (
    .in0(Operand2), .in1(Immediate), .out(multiplexer_4_out), .sel(ExecutePipelineStage_1_ram_src_out));
  and and_2 (and_2_out, ExecutePipelineStage_1_is_ramop_out, InstrExec);
  Bit_Extender #(.in_width(16), .out_width(4)) bit_extender_1 (.in(Immediate), .out(bit_extender_1_out));
  Bit_Extender #(.in_width(16), .out_width(4)) bit_extender_2 (.in(Immediate), .out(bit_extender_2_out));
  Adder #(.width(16)) adder_1 (
    .a(ExecutePipelineStage_1_ma_out), .b(multiplexer_4_out), .out(adder_1_out));  // open: cin, cout
  RAM #(.addrWidth(16), .dataWidth(16)) RAM_1 (
    .addr(multiplexer_5_out), .we(ExecutePipelineStage_1_ram_write_out),
    .oe(ExecutePipelineStage_1_ram_read_out), .clk(and_2_out), .din(Operand1), .dout(RAM_1_dout));
  Multiplexer #(.width(16)) multiplexer_5 (
    .in0(multiplexer_4_out), .in1(adder_1_out), .out(multiplexer_5_out),
    .sel(ExecutePipelineStage_1_use_ma_out));
  IM_Modifier im_modifier_1 (
    .Reg1_Read(Operand1), .Immediate(Immediate), .IMH(ExecutePipelineStage_1_whb_out),
    .IML(ExecutePipelineStage_1_wlb_out), .Union(im_modifier_1_union));
  ALU ALU_1 (
    .ALU_Function(bit_extender_2_out), .Operand1(Operand1), .Operand2(Operand2),
    .ALU_Output(ALU_1_alu_output), .ALU_Flags(ALU_1_alu_flags));
  JumpController JumpController_1 (
    .JMP(ExecutePipelineStage_1_jmp_out), .JMP_Condintional(ExecutePipelineStage_1_jmp_condintional_out),
    .JMP_Relative(ExecutePipelineStage_1_jmp_relative_out),
    .JMP_ConditionalMode(ExecutePipelineStage_1_jmp_condition_out), .Flags(Operand2),
    .JumpAddress(Immediate), .PC_In(counter_1_q), .PC_DIn(JMP_PC_In), .PC_Out(JMP_PC_Addr));
  ExternalDeviceController ExternalDeviceController_1 (
    .ControlExternalDevice(ExecutePipelineStage_1_is_extop_out), .ExternalDeviceID(bit_extender_1_out),
    .ExternalArgument1(Operand1), .ExternalArgument2(Operand2), .CLK(InstrExec),
    .EXT0_D1(ExternalDeviceController_1_ext0_d1), .EXT0_CLK(ExternalDeviceController_1_ext0_clk),
    .EXT1_D0(ExternalDeviceController_1_ext1_d0), .EXT1_D1(ExternalDeviceController_1_ext1_d1),
    .EXT1_CLK(ExternalDeviceController_1_ext1_clk), .EXT0_D0(ExternalDeviceController_1_ext0_d0));  // open: EXT2_D0, EXT2_D1, EXT2_CLK, EXT3_D0, EXT3_D1, EXT3_CLK, EXT4_D0, EXT4_D1, EXT4_CLK
  SignedNumberDisplay SignedNumberDisplay_1 (
    .D0(ExternalDeviceController_1_ext0_d0), .D1(ExternalDeviceController_1_ext0_d1),
    .CLK(ExternalDeviceController_1_ext0_clk));
  Multiplexer #(.select(2), .width(16)) multiplexer_6 (
    .in0(RAM_1_dout), .in1(im_modifier_1_union), .in2(Operand1), .in3(ALU_1_alu_output),
    .out(multiplexer_6_out), .sel(ExecutePipelineStage_1_din_sel_out));
  VGAController VGAController_1 (
    .EXT0_A0(ExternalDeviceController_1_ext1_d0), .EXT0_A1(ExternalDeviceController_1_ext1_d1),
    .EXT0_CLK(ExternalDeviceController_1_ext1_clk), .PixX(VGAController_1_pixx), .PixY(VGAController_1_pixy),
    .RGB(VGAController_1_rgb), .CLK_Out(VGAController_1_clk_out));
  WriteBackPipelineStage WriteBackPipelineStage_1 (
    .InstrLoad(InstrLoad), .Reset(Reset), .WriteAddress(ExecutePipelineStage_1_writeaddress_out),
    .WriteData(multiplexer_6_out), .Flags(ALU_1_alu_flags), .WHB(ExecutePipelineStage_1_whb_out),
    .WLB(ExecutePipelineStage_1_wlb_out), .Is_ALUOP(ExecutePipelineStage_1_is_aluop_out),
    .JMP(ExecutePipelineStage_1_jmp_out), .WriteAddress_out(WriteBackPipelineStage_1_writeaddress_out),
    .WriteData_out(WriteBackPipelineStage_1_writedata_out), .Flags_out(WriteBackPipelineStage_1_flags_out),
    .WHB_out(WriteBackPipelineStage_1_whb_out), .WLB_out(WriteBackPipelineStage_1_wlb_out),
    .IS_ALUOP_out(WriteBackPipelineStage_1_is_aluop_out), .JMP_out(WriteBackPipelineStage_1_jmp_out));
  Button Button_2 (.out(Button_2_out));
  // RGB_Video #(.cursor("No Cursor"), .height(256), .width(256)) rgb_video_1: pin names not known; wires that end beside it: Button_2_out, VGAController_1_clk_out, 1'b1, VGAController_1_pixx, VGAController_1_pixy, VGAController_1_rgb

  // Notes on the sheet:
  //   contents of ROM_1 (hex, n*v repeats v):
  //   4000 5000 4101 5100 4300 5300 4401 5400 e200 e001 7230 1002 8005 e10e 1034 e30e a008 4000 5000 1130
  //   8406 6100 f011 1004 e00e a013
endmodule

module ALU (
  input  [3:0] ALU_Function,
  input  [15:0] Operand1,
  input  [15:0] Operand2,
  output [15:0] ALU_Output,
  output [15:0] ALU_Flags
);

  wire and_1_out, and_2_out, ArithmeticUnit_1_carryout, ArithmeticUnit_1_overflow, nor_1_out, nor_2_out;
  wire [15:0] ArithmeticUnit_1_arithmetic_out, LogicUnit_1_logicalout;

  and and_1 (and_1_out, ~ALU_Function[3], ArithmeticUnit_1_carryout);  // AND_Gate
  ArithmeticUnit ArithmeticUnit_1 (
    .ALU_Function(ALU_Function), .Operand1(Operand1), .Operand2(Operand2),
    .Arithmetic_Out(ArithmeticUnit_1_arithmetic_out), .CarryOut(ArithmeticUnit_1_carryout),
    .Overflow(ArithmeticUnit_1_overflow));
  and and_2 (and_2_out, ~ALU_Function[3], ArithmeticUnit_1_overflow);  // AND_Gate
  LogicUnit LogicUnit_1 (
    .ALU_Function(ALU_Function), .Operand1(Operand1), .Operand2(Operand2), .LogicalOut(LogicUnit_1_logicalout));
  Multiplexer #(.width(16)) multiplexer_1 (
    .in0(ArithmeticUnit_1_arithmetic_out), .in1(LogicUnit_1_logicalout), .out(ALU_Output),
    .sel(ALU_Function[3]));
  nor nor_1 (nor_1_out, ALU_Output[0], ALU_Output[1], ALU_Output[2], ALU_Output[3], ALU_Output[4], ALU_Output[5], ALU_Output[6], ALU_Output[7], ALU_Output[9], ALU_Output[10], ALU_Output[11], ALU_Output[12], ALU_Output[13], ALU_Output[14], ALU_Output[15], ALU_Output[8]);
  nor nor_2 (nor_2_out, ALU_Output[15], nor_1_out);
  ALUFlagPacker ALUFlagPacker_1 (
    .CarryFlag(and_1_out), .ZeroFlag(nor_1_out), .SmallerZero(ALU_Output[15]), .BiggerZero(nor_2_out),
    .Overflow(and_2_out), .BoolFlag(ALU_Output[0]), .PackedFlags(ALU_Flags));
endmodule

module LogicUnit (
  input  [3:0] ALU_Function,
  input  [15:0] Operand1,
  input  [15:0] Operand2,
  output [15:0] LogicalOut
);

  wire [15:0] and_1_out, bit_extender_1_out, multiplexer_1_out, or_1_out, xor_1_out;

  assign and_1_out = Operand1 & Operand2;  // AND_Gate and_1, 16 bits wide
  assign or_1_out = Operand1 | Operand2;  // OR_Gate or_1, 16 bits wide
  assign xor_1_out = Operand1 ^ Operand2;  // XOR_Gate xor_1, 16 bits wide
  Multiplexer #(.select(2), .width(16)) multiplexer_1 (
    .in0(Operand1), .in1(and_1_out), .in2(or_1_out), .in3(xor_1_out), .out(multiplexer_1_out),
    .sel(ALU_Function[1:0]));
  assign bit_extender_1_out = {{15{ALU_Function[2]}}, ALU_Function[2]};  // Bit_Extender bit_extender_1
  assign LogicalOut = bit_extender_1_out ^ multiplexer_1_out;  // XOR_Gate xor_2, 16 bits wide

  // Other names for the same wires on the sheet: LogicalFunction[1:0] = ALU_Function[1:0]; Inverted = ALU_Function[2]
endmodule

module ArithmeticUnit (
  input  [3:0] ALU_Function,
  input  [15:0] Operand1,
  input  [15:0] Operand2,
  output [15:0] Arithmetic_Out,
  output CarryOut,
  output Overflow
);

  wire adder_1_cout, subtractor_1_bout, xnor_1_out, xor_1_out, xor_2_out;
  wire [3:0] bit_extender_1_out;
  wire [15:0] adder_1_out, shifter_1_out, shifter_2_out, subtractor_1_out;

  Bit_Extender #(.in_width(16), .out_width(4)) bit_extender_1 (.in(Operand2), .out(bit_extender_1_out));
  Adder #(.width(16)) adder_1 (.a(Operand1), .b(Operand2), .out(adder_1_out), .cout(adder_1_cout));  // open: cin
  Subtractor #(.width(16)) subtractor_1 (
    .a(Operand1), .b(Operand2), .out(subtractor_1_out), .bout(subtractor_1_bout));  // open: bin
  Shifter #(.width(16)) shifter_1 (.in(Operand1), .\dist (bit_extender_1_out), .out(shifter_1_out));
  Shifter #(.shift("lr"), .width(16)) shifter_2 (.in(Operand1), .\dist (bit_extender_1_out), .out(shifter_2_out));
  xor xor_1 (xor_1_out, ALU_Function[0], Operand2[15]);
  xnor xnor_1 (xnor_1_out, xor_1_out, Operand1[15]);
  xor xor_2 (xor_2_out, Operand1[15], Arithmetic_Out[15]);
  Multiplexer #(.select(3), .width(16)) multiplexer_1 (
    .in0(adder_1_out), .in1(subtractor_1_out), .in2(shifter_1_out), .in3(shifter_2_out), .in4({16{1'b0}}),
    .in5({16{1'b0}}), .in6({16{1'b0}}), .in7({16{1'b0}}), .out(Arithmetic_Out), .sel(ALU_Function[2:0]));
  Multiplexer #(.select(3)) multiplexer_2 (
    .in0(adder_1_cout), .in1(subtractor_1_bout), .in2(1'b0), .in3(1'b0), .in4(1'b0), .in5(1'b0), .in6(1'b0),
    .in7(1'b0), .out(CarryOut), .sel(ALU_Function[2:0]));
  and and_1 (Overflow, xnor_1_out, xor_2_out);

  // Other names for the same wires on the sheet: MathFunction[2:0] = ALU_Function[2:0]; S = ALU_Function[0];
  //   Y15 = Arithmetic_Out[15]; A15 = Operand1[15]; B15 = Operand2[15]
endmodule

module ALUFlagPacker (
  input  CarryFlag,
  input  ZeroFlag,
  input  SmallerZero,
  input  BiggerZero,
  input  Overflow,
  input  BoolFlag,
  output [15:0] PackedFlags
);


  assign PackedFlags = {{10{1'b0}}, BoolFlag, Overflow, BiggerZero, SmallerZero, ZeroFlag, CarryFlag};
endmodule

module ALUFlagUnpacker (
  input  [15:0] PackedFlags,
  output CarryFlag,
  output ZeroFlag,
  output SmallerZero,
  output BiggerZero,
  output Overflow,
  output BoolFlag
);


  assign BiggerZero = PackedFlags[3];
  assign BoolFlag = PackedFlags[5];
  assign CarryFlag = PackedFlags[0];
  assign Overflow = PackedFlags[4];
  assign SmallerZero = PackedFlags[2];
  assign ZeroFlag = PackedFlags[1];
endmodule

module RegFile (
  input  [15:0] WriteData,
  input  WHB,
  input  WLB,
  input  CLK,
  input  [3:0] ReadAddress1,
  input  [3:0] ReadAddress2,
  input  [3:0] WriteAddress,
  input  [15:0] Flags,
  input  IsALUOP,
  output [15:0] Operand1,
  output [15:0] Operand2,
  output [15:0] MA
);

  wire and_1_out, decoder_1_out0, decoder_1_out1, decoder_1_out2, decoder_1_out3, decoder_1_out4,
       decoder_1_out5, decoder_1_out6, decoder_1_out7, decoder_1_out8, decoder_1_out9, decoder_1_out10,
       decoder_1_out11, decoder_1_out12, decoder_1_out13, decoder_1_out14, or_1_out;
  wire [7:0] multiplexer_1_out, multiplexer_2_out, multiplexer_3_out;
  wire [15:0] register_1_q, register_2_q, register_3_q, register_4_q, register_5_q, register_6_q,
       register_7_q, register_8_q, register_9_q, register_10_q, register_12_q, register_13_q, register_14_q,
       register_15_q, register_16_q, WriteRegisterValue;

  Decoder #(.select(4)) decoder_1 (
    .out0(decoder_1_out0), .out1(decoder_1_out1), .out2(decoder_1_out2), .out3(decoder_1_out3),
    .out4(decoder_1_out4), .out5(decoder_1_out5), .out6(decoder_1_out6), .out7(decoder_1_out7),
    .out8(decoder_1_out8), .out9(decoder_1_out9), .out10(decoder_1_out10), .out11(decoder_1_out11),
    .out12(decoder_1_out12), .out13(decoder_1_out13), .out14(decoder_1_out14), .sel(WriteAddress));  // open: out15, en
  Multiplexer #(.width(8)) multiplexer_1 (
    .in0(WriteData[7:0]), .in1(WriteData[15:8]), .out(multiplexer_1_out), .sel(WLB));
  or or_1 (or_1_out, WHB, WLB);
  Multiplexer #(.width(8)) multiplexer_2 (
    .in0(WriteRegisterValue[15:8]), .in1(multiplexer_1_out), .out(multiplexer_2_out), .sel(WHB));
  Multiplexer #(.width(8)) multiplexer_3 (
    .in0(WriteRegisterValue[7:0]), .in1(WriteData[7:0]), .out(multiplexer_3_out), .sel(WLB));
  and and_1 (and_1_out, or_1_out, CLK);
  Register #(.width(16)) register_1 (
    .D(WriteData), .en(decoder_1_out0), .Q(register_1_q), .clk(and_1_out));  // open: clr
  Register #(.width(16)) register_2 (
    .D(WriteData), .en(decoder_1_out1), .Q(register_2_q), .clk(and_1_out));  // open: clr
  Register #(.width(16)) register_3 (
    .D(WriteData), .en(decoder_1_out2), .Q(register_3_q), .clk(and_1_out));  // open: clr
  Register #(.width(16)) register_4 (
    .D(WriteData), .en(decoder_1_out3), .Q(register_4_q), .clk(and_1_out));  // open: clr
  Register #(.width(16)) register_5 (
    .D(WriteData), .en(decoder_1_out4), .Q(register_5_q), .clk(and_1_out));  // open: clr
  Register #(.width(16)) register_6 (
    .D(WriteData), .en(decoder_1_out5), .Q(register_6_q), .clk(and_1_out));  // open: clr
  Register #(.width(16)) register_7 (
    .D(WriteData), .en(decoder_1_out6), .Q(register_7_q), .clk(and_1_out));  // open: clr
  Register #(.width(16)) register_8 (
    .D(WriteData), .en(decoder_1_out7), .Q(register_8_q), .clk(and_1_out));  // open: clr
  Register #(.width(16)) register_9 (
    .D(WriteData), .en(decoder_1_out8), .Q(register_9_q), .clk(and_1_out));  // open: clr
  Register #(.width(16)) register_10 (
    .D(WriteData), .en(decoder_1_out9), .Q(register_10_q), .clk(and_1_out));  // open: clr
  Register #(.width(16)) register_11 (.D(WriteData), .en(decoder_1_out10), .Q(MA), .clk(and_1_out));  // open: clr
  Register #(.width(16)) register_12 (
    .D(WriteData), .en(decoder_1_out11), .Q(register_12_q), .clk(and_1_out));  // open: clr
  Register #(.width(16)) register_13 (
    .D(WriteData), .en(decoder_1_out12), .Q(register_13_q), .clk(and_1_out));  // open: clr
  Register #(.width(16)) register_14 (
    .D(WriteData), .en(decoder_1_out13), .Q(register_14_q), .clk(and_1_out));  // open: clr
  Register #(.width(16)) register_15 (
    .D(WriteData), .en(decoder_1_out14), .Q(register_15_q), .clk(and_1_out));  // open: clr
  Register #(.width(16)) register_16 (.D(Flags), .en(IsALUOP), .Q(register_16_q), .clk(CLK));  // open: clr
  Multiplexer #(.select(4), .width(16)) multiplexer_4 (
    .in0(register_1_q), .in1(register_2_q), .in2(register_3_q), .in3(register_4_q), .in4(register_5_q),
    .in5(register_6_q), .in6(register_7_q), .in7(register_8_q), .in8(register_9_q), .in9(register_10_q),
    .in10(MA), .in11(register_12_q), .in12(register_13_q), .in13(register_14_q), .in14(register_15_q),
    .in15(register_16_q), .out(WriteRegisterValue), .sel(WriteAddress));
  Multiplexer #(.select(4), .width(16)) multiplexer_5 (
    .in0(register_1_q), .in1(register_2_q), .in2(register_3_q), .in3(register_4_q), .in4(register_5_q),
    .in5(register_6_q), .in6(register_7_q), .in7(register_8_q), .in8(register_9_q), .in9(register_10_q),
    .in10(MA), .in11(register_12_q), .in12(register_13_q), .in13(register_14_q), .in14(register_15_q),
    .in15(register_16_q), .out(Operand1), .sel(ReadAddress1));
  Multiplexer #(.select(4), .width(16)) multiplexer_6 (
    .in0(register_1_q), .in1(register_2_q), .in2(register_3_q), .in3(register_4_q), .in4(register_5_q),
    .in5(register_6_q), .in6(register_7_q), .in7(register_8_q), .in8(register_9_q), .in9(register_10_q),
    .in10(MA), .in11(register_12_q), .in12(register_13_q), .in13(register_14_q), .in14(register_15_q),
    .in15(register_16_q), .out(Operand2), .sel(ReadAddress2));

  // Other names for the same wires on the sheet: Raw_CLK = CLK
endmodule

module InstructionDecoder (
  input  [15:0] Instruction,
  output [3:0] Reg1,
  output Reg1Read,
  output [3:0] Reg2,
  output Reg2Read,
  output [3:0] WriteReg,
  output [15:0] Immediate,
  output RF_WHB,
  output RF_WLB,
  output [1:0] DIn_Sel,
  output RAM_Src,
  output RAM_Read,
  output RAM_Write,
  output USE_MA,
  output JMP,
  output JMP_Condintional,
  output JMP_Relative,
  output [2:0] JMP_ConditionalMode,
  output IsALUOP,
  output IsRAMOP,
  output IsEXTOP
);

  wire comparator_1_eq, comparator_2_eq, comparator_3_eq, comparator_4_eq, comparator_5_eq, comparator_6_eq,
       comparator_7_eq, comparator_9_eq, comparator_10_eq, decoder_1_out1, decoder_1_out3, decoder_1_out4,
       decoder_1_out5, decoder_1_out7, decoder_1_out14, decoder_1_out15, decoder_2_out1, decoder_2_out6,
       decoder_2_out7, decoder_2_out8, decoder_2_out15, or_1_out, or_4_out;
  wire [15:0] bit_extender_1_out, bit_extender_2_out, bit_extender_3_out, bit_extender_4_out,
       bit_extender_5_out, bit_extender_6_out, bit_extender_7_out;

  Comparator #(.mode("unsigned"), .width(4)) comparator_1 (
    .a(Instruction[15:12]), .b(4'b0100), .eq(comparator_1_eq));  // open: gt, lt
  Comparator #(.mode("unsigned"), .width(4)) comparator_2 (
    .a(Instruction[15:12]), .b(4'b0101), .eq(comparator_2_eq));  // open: gt, lt
  Comparator #(.mode("unsigned"), .width(4)) comparator_3 (
    .a(Instruction[15:12]), .b(4'b0010), .eq(comparator_3_eq));  // open: gt, lt
  Comparator #(.mode("unsigned"), .width(4)) comparator_4 (
    .a(Instruction[15:12]), .b(4'b0110), .eq(comparator_4_eq));  // open: gt, lt
  Comparator #(.mode("unsigned"), .width(4)) comparator_5 (
    .a(Instruction[15:12]), .b(4'b0011), .eq(comparator_5_eq));  // open: gt, lt
  Comparator #(.mode("unsigned"), .width(4)) comparator_6 (
    .a(Instruction[15:12]), .b(4'b0111), .eq(comparator_6_eq));  // open: gt, lt
  Comparator #(.mode("unsigned"), .width(4)) comparator_7 (
    .a(Instruction[15:12]), .b(4'b1110), .eq(comparator_7_eq));  // open: gt, lt
  Comparator #(.mode("unsigned"), .width(4)) comparator_8 (
    .a(Instruction[15:12]), .b(4'b1000), .eq(JMP_Condintional));  // open: gt, lt
  Comparator #(.mode("unsigned"), .width(4)) comparator_9 (
    .a(Instruction[15:12]), .b(4'b1001), .eq(comparator_9_eq));  // open: gt, lt
  Comparator #(.mode("unsigned"), .width(4)) comparator_10 (
    .a(Instruction[15:12]), .b(4'b1010), .eq(comparator_10_eq));  // open: gt, lt
  Comparator #(.mode("unsigned"), .width(4)) comparator_11 (
    .a(Instruction[15:12]), .b(4'b0001), .eq(IsALUOP));  // open: gt, lt
  Comparator #(.mode("unsigned"), .width(4)) comparator_12 (
    .a(Instruction[15:12]), .b(4'b1111), .eq(IsEXTOP));  // open: gt, lt
  or or_1 (or_1_out, comparator_6_eq, comparator_3_eq);
  or or_2 (RF_WLB, comparator_1_eq, comparator_3_eq, IsALUOP, comparator_4_eq, comparator_7_eq);
  or or_3 (RF_WHB, comparator_2_eq, comparator_3_eq, IsALUOP, comparator_4_eq, comparator_7_eq);
  or or_4 (or_4_out, comparator_2_eq, comparator_1_eq);
  or or_5 (RAM_Read, comparator_4_eq, comparator_3_eq);
  or or_6 (RAM_Src, comparator_3_eq, comparator_5_eq);
  or or_7 (RAM_Write, comparator_5_eq, comparator_6_eq);
  and and_1 (USE_MA, or_1_out, Instruction[0]);
  or or_8 (JMP, JMP_Condintional, comparator_9_eq, comparator_10_eq);
  or or_9 (JMP_Relative, JMP_Condintional, comparator_9_eq);
  or or_10 (IsRAMOP, RAM_Read, RAM_Write);
  Priority_Encoder #(.select(2)) priority_encoder_1 (
    .in0(IsRAMOP), .in1(or_4_out), .in2(comparator_7_eq), .in3(IsALUOP), .out(DIn_Sel));  // open: gs, en_out, en_in
  assign bit_extender_1_out = {{12{1'b0}}, Instruction[11:8]};  // Bit_Extender bit_extender_1
  assign bit_extender_2_out = {{8{1'b0}}, Instruction[7:0]};  // Bit_Extender bit_extender_2
  assign bit_extender_3_out = {{8{1'b0}}, Instruction[7:0]};  // Bit_Extender bit_extender_3
  assign bit_extender_4_out = {{7{Instruction[8]}}, Instruction[8:0]};  // Bit_Extender bit_extender_4
  assign bit_extender_5_out = {{4{Instruction[11]}}, Instruction[11:0]};  // Bit_Extender bit_extender_5
  assign bit_extender_6_out = {{4{1'b0}}, Instruction[11:0]};  // Bit_Extender bit_extender_6
  assign bit_extender_7_out = {{12{1'b0}}, Instruction[11:8]};  // Bit_Extender bit_extender_7
  Multiplexer #(.select(4), .width(4)) multiplexer_1 (
    .in0(4'b0000), .in1(Instruction[7:4]), .in2(4'b0000), .in3(Instruction[11:8]), .in4(Instruction[11:8]),
    .in5(Instruction[11:8]), .in6(4'b0000), .in7(Instruction[11:8]), .in8(4'b0000), .in9(4'b0000),
    .in10(4'b0000), .in11(4'b0000), .in12(4'b0000), .in13(4'b0000), .in14(Instruction[3:0]),
    .in15(Instruction[7:4]), .out(Reg1), .sel(Instruction[15:12]));
  Multiplexer #(.select(4), .width(4)) multiplexer_2 (
    .in0(4'b0000), .in1(Instruction[3:0]), .in2(4'b0000), .in3(4'b0000), .in4(4'b0000), .in5(4'b0000),
    .in6(Instruction[7:4]), .in7(Instruction[7:4]), .in8(4'b1111), .in9(4'b0000), .in10(4'b0000),
    .in11(4'b0000), .in12(4'b0000), .in13(4'b0000), .in14(4'b0000), .in15(Instruction[3:0]), .out(Reg2),
    .sel(Instruction[15:12]));
  Multiplexer #(.select(4), .width(4)) multiplexer_3 (
    .in0(4'b0000), .in1(4'b1110), .in2(Instruction[11:8]), .in3(4'b0000), .in4(Instruction[11:8]),
    .in5(Instruction[11:8]), .in6(Instruction[11:8]), .in7(4'b0000), .in8(4'b0000), .in9(4'b0000),
    .in10(4'b0000), .in11(4'b0000), .in12(4'b0000), .in13(4'b0000), .in14(Instruction[11:8]), .in15(4'b0000),
    .out(WriteReg), .sel(Instruction[15:12]));
  Multiplexer #(.select(4), .width(16)) multiplexer_4 (
    .in0({16{1'b0}}), .in1(bit_extender_1_out), .in2(bit_extender_2_out), .in3(bit_extender_2_out),
    .in4(bit_extender_3_out), .in5({16{1'b0}}), .in6({16{1'b0}}), .in7({16{1'b0}}), .in8(bit_extender_4_out),
    .in9(bit_extender_5_out), .in10(bit_extender_6_out), .in11({16{1'b0}}), .in12({16{1'b0}}),
    .in13({16{1'b0}}), .in14({16{1'b0}}), .in15(bit_extender_7_out), .out(Immediate), .sel(Instruction[15:12]));
  Decoder #(.enable("false"), .select(4)) decoder_1 (
    .out1(decoder_1_out1), .out3(decoder_1_out3), .out4(decoder_1_out4), .out5(decoder_1_out5),
    .out7(decoder_1_out7), .out14(decoder_1_out14), .out15(decoder_1_out15), .sel(Instruction[15:12]));  // open: out0, out2, out6, out8, out9, out10, out11, out12, out13
  Decoder #(.enable("false"), .select(4)) decoder_2 (
    .out1(decoder_2_out1), .out6(decoder_2_out6), .out7(decoder_2_out7), .out8(decoder_2_out8),
    .out15(decoder_2_out15), .sel(Instruction[15:12]));  // open: out0, out2, out3, out4, out5, out9, out10, out11, out12, out13, out14
  or or_11 (Reg1Read, decoder_1_out1, decoder_1_out3, decoder_1_out4, decoder_1_out5, decoder_1_out7, decoder_1_out14, decoder_1_out15);
  or or_12 (Reg2Read, decoder_2_out1, decoder_2_out6, decoder_2_out7, decoder_2_out8, decoder_2_out15);

  assign JMP_ConditionalMode = Instruction[11:9];

  // Other names for the same wires on the sheet: RawInstr[15:0] = Instruction;
  //   InstructionName[3:0] = Instruction[15:12]

  // Notes on the sheet:
  //   $FL for Conditional Jumps
endmodule

module ExternalDeviceController (
  input  ControlExternalDevice,
  input  [3:0] ExternalDeviceID,
  input  [15:0] ExternalArgument1,
  input  [15:0] ExternalArgument2,
  input  CLK,
  output [15:0] EXT0_D0,
  output [15:0] EXT0_D1,
  output EXT0_CLK,
  output [15:0] EXT1_D0,
  output [15:0] EXT1_D1,
  output EXT1_CLK,
  output [15:0] EXT2_D0,
  output [15:0] EXT2_D1,
  output EXT2_CLK,
  output [15:0] EXT3_D0,
  output [15:0] EXT3_D1,
  output EXT3_CLK,
  output [15:0] EXT4_D0,
  output [15:0] EXT4_D1,
  output EXT4_CLK
);

  wire decoder_1_out0, decoder_1_out1, decoder_1_out2, decoder_1_out3, decoder_1_out4;

  Decoder #(.select(4)) decoder_1 (
    .out0(decoder_1_out0), .out1(decoder_1_out1), .out2(decoder_1_out2), .out3(decoder_1_out3),
    .out4(decoder_1_out4), .sel(ExternalDeviceID), .en(ControlExternalDevice));  // open: out5, out6, out7, out8, out9, out10, out11, out12, out13, out14, out15
  and and_1 (EXT0_CLK, decoder_1_out0, CLK);
  and and_2 (EXT1_CLK, decoder_1_out1, CLK);
  and and_3 (EXT2_CLK, decoder_1_out2, CLK);
  and and_4 (EXT3_CLK, decoder_1_out3, CLK);
  and and_5 (EXT4_CLK, decoder_1_out4, CLK);

  assign EXT0_D0 = ExternalArgument1;
  assign EXT0_D1 = ExternalArgument2;
  assign EXT1_D0 = ExternalArgument1;
  assign EXT1_D1 = ExternalArgument2;
  assign EXT2_D0 = ExternalArgument1;
  assign EXT2_D1 = ExternalArgument2;
  assign EXT3_D0 = ExternalArgument1;
  assign EXT3_D1 = ExternalArgument2;
  assign EXT4_D0 = ExternalArgument1;
  assign EXT4_D1 = ExternalArgument2;

  // Other names for the same wires on the sheet: EA1[15:0] = ExternalArgument1; EA2[15:0] = ExternalArgument2
endmodule

module SignedNumberDisplay (
  input  [15:0] D0,
  input  [15:0] D1,
  input  CLK
);

  wire [15:0] register_1_q;
  wire [20:0] ROM_1_data;

  Register #(.width(16)) register_1 (.D(D0), .clk(CLK), .Q(register_1_q));  // open: en, clr
  ROM #(.addrWidth(16), .dataWidth(21)) ROM_1 (.addr(register_1_q), .data(ROM_1_data));
  _7_Segment_Display L_7_Segment_Display_1 (.g(ROM_1_data[20]));  // open: f, a, b, e, d, c, dp
  Hex_Digit_Display Hex_Digit_Display_2 (.value(ROM_1_data[15:12]));  // open: dp
  Hex_Digit_Display Hex_Digit_Display_1 (.value(ROM_1_data[19:16]));  // open: dp
  Hex_Digit_Display Hex_Digit_Display_3 (.value(ROM_1_data[11:8]));  // open: dp
  Hex_Digit_Display Hex_Digit_Display_4 (.value(ROM_1_data[7:4]));  // open: dp
  Hex_Digit_Display Hex_Digit_Display_5 (.value(ROM_1_data[3:0]));  // open: dp

  // Notes on the sheet:
  //   contents of ROM_1 (hex, n*v repeats v):
  //   0 1 2 3 4 5 6 7 8 9 10 11 12 13 14 15 16 17 18 19 20 21 22 23 24 25 26 27 28 29 30 31 32 33 34 35 36
  //   37 38 39 40 41 42 43 44 45 46 47 48 49 50 51 52 53 54 55 56 57 58 59 60 61 62 63 64 65 66 67 68 69
  //   70 71 72 73 74 75 76 77 78 79 80 81 82 83 84 85 86 87 88 89 90 91 92 93 94 95 96 97 98 99 100 101
  //   102 103 104 105 106 107 108 109 110 111 112 113 114 115 116 117 118 119 120 121 122 123 124 125 126
  //   127 128 129 130 131 132 133 134 135 136 137 138 139 140 141 142 143 144 145 146 147 148 149 150 151
  //   152 153 154 155 156 157 158 159 160 161 162 163 164 165 166 167 168 169 170 171 172 173 174 175 176
  //   177 178 179 180 181 182 183 184 185 186 187 188 189 190 191 192 193 194 195 196 197 198 199 200 201
  //   202 203 204 205 206 207 208 209 210 211 212 213 214 215 216 217 218 219 220 221 222 223 224 225 226
  //   227 228 229 230 231 232 233 234 235 236 237 238 239 240 241 242 243 244 245 246 247 248 249 250 251
  //   252 253 254 255 256 257 258 259 260 261 262 263 264 265 266 267 268 269 270 271 272 273 274 275 276
  //   277 278 279 280 281 282 283 284 285 286 287 288 289 290 291 292 293 294 295 296 297 298 299 300 301
  //   302 303 304 305 306 307 308 309 310 311 312 313 314 315 316 317 318 319 320 321 322 323 324 325 326
  //   327 328 329 330 331 332 333 334 335 336 337 338 339 340 341 342 343 344 345 346 347 348 349 350 351
  //   352 353 354 355 356 357 358 359 360 361 362 363 364 365 366 367 368 369 370 371 372 373 374 375 376
  //   377 378 379 380 381 382 383 384 385 386 387 388 389 390 391 392 393 394 395 396 397 398 399 400 401
  //   402 403 404 405 406 407 408 409 410 411 412 413 414 415 416 417 418 419 420 421 422 423 424 425 426
  //   427 428 429 430 431 432 433 434 435 436 437 438 439 440 441 442 443 444 445 446 447 448 449 450 451
  //   452 453 454 455 456 457 458 459 460 461 462 463 464 465 466 467 468 469 470 471 472 473 474 475 476
  //   477 478 479 480 481 482 483 484 485 486 487 488 489 490 491 492 493 494 495 496 497 498 499 500 501
  //   502 503 504 505 506 507 508 509 510 511 512 513 514 515 516 517 518 519 520 521 522 523 524 525 526
  //   527 528 529 530 531 532 533 534 535 536 537 538 539 540 541 542 543 544 545 546 547 548 549 550 551
  //   552 553 554 555 556 557 558 559 560 561 562 563 564 565 566 567 568 569 570 571 572 573 574 575 576
  //   577 578 579 580 581 582 583 584 585 586 587 588 589 590 591 592 593 594 595 596 597 598 599 600 601
  //   602 603 604 605 606 607 608 609 610 611 612 613 614 615 616 617 618 619 620 621 622 623 624 625 626
  //   627 628 629 630 631 632 633 634 635 636 637 638 639 640 641 642 643 644 645 646 647 648 649 650 651
  //   652 653 654 655 656 657 658 659 660 661 662 663 664 665 666 667 668 669 670 671 672 673 674 675 676
  //   677 678 679 680 681 682 683 684 685 686 687 688 689 690 691 692 693 694 695 696 697 698 699 700 701
  //   702 703 704 705 706 707 708 709 710 711 712 713 714 715 716 717 718 719 720 721 722 723 724 725 726
  //   727 728 729 730 731 732 733 734 735 736 737 738 739 740 741 742 743 744 745 746 747 748 749 750 751
  //   752 753 754 755 756 757 758 759 760 761 762 763 764 765 766 767 768 769 770 771 772 773 774 775 776
  //   777 778 779 780 781 782 783 784 785 786 787 788 789 790 791 792 793 794 795 796 797 798 799 800 801
  //   802 803 804 805 806 807 808 809 810 811 812 813 814 815 816 817 818 819 820 821 822 823 824 825 826
  //   827 828 829 830 831 832 833 834 835 836 837 838 839 840 841 842 843 844 845 846 847 848 849 850 851
  //   852 853 854 855 856 857 858 859 860 861 862 863 864 865 866 867 868 869 870 871 872 873 874 875 876
  //   877 878 879 880 881 882 883 884 885 886 887 888 889 890 891 892 893 894 895 896 897 898 899 900 901
  //   902 903 904 905 906 907 908 909 910 911 912 913 914 915 916 917 918 919 920 921 922 923 924 925 926
  //   927 928 929 930 931 932 933 934 935 936 937 938 939 940 941 942 943 944 945 946 947 948 949 950 951
  //   952 953 954 955 956 957 958 959 960 961 962 963 964 965 966 967 968 969 970 971 972 973 974 975 976
  //   977 978 979 980 981 982 983 984 985 986 987 988 989 990 991 992 993 994 995 996 997 998 999 1000
  //   1001 1002 1003 1004 1005 1006 1007 1008 1009 1010 1011 1012 1013 1014 1015 1016 1017 1018 1019 1020
  //   1021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
endmodule

module ClockController (
  input  RawCLK,
  output InstrLoad,
  output InstrExec
);

  wire and_1_out, and_2_out, not_1_out, not_2_out, not_3_out, undriven;

  not not_1 (not_1_out, undriven);
  not not_2 (not_2_out, undriven);
  and and_1 (and_1_out, undriven, not_1_out);
  and and_2 (and_2_out, not_1_out, not_3_out);
  not not_3 (not_3_out, not_2_out);
  not not_4 (InstrExec, RawCLK);

  assign InstrLoad = RawCLK;
endmodule

module PipeliningController (
  input  InstrLoad,
  input  InstrExec,
  input  Reset,
  input  [15:0] InstructionIn,
  input  ResolveStall,
  output PC_CLK,
  output [4:0] InstructionForwarding,
  output [15:0] QueryInstruction
);

  wire and_1_out, and_3_out, and_12_out, and_13_out, and_14_out, and_15_out, comparator_1_eq,
       comparator_2_eq, comparator_3_eq, comparator_4_eq, comparator_5_eq, Exc_ALU, Exc_Write, IE_Flank,
       IL_Flank, InstructionDecoder_2_rf_whb, InstructionDecoder_2_rf_wlb, MA_ReadsExcResults, not_1_out,
       not_2_out, or_2_out, or_3_out, Reg1_ReadsExcResults, Reg1_ReadsFlags, Reg2_ReadsExcResults,
       Reg2_ReadsFlags, RF_Reg1_Read, RF_Reg2_Read, shift_register_1_p2, shift_register_1_p3, Stalled,
       StallRequired, USE_MA;
  wire [1:0] priority_encoder_1_out, priority_encoder_2_out;
  wire [3:0] Exc_WriteAddr, RF_Reg1, RF_Reg2;
  wire [4:4] priority_encoder_3_out;
  wire [15:0] shift_register_1_p6, shift_register_1_p7, shift_register_1_p9;

  and and_1 (and_1_out, IE_Flank, ResolveStall);
  not not_1 (not_1_out, InstrLoad);
  not not_2 (not_2_out, InstrExec);
  // Shift_Register #(.length(4), .width(16)) shift_register_1: pin names not known; wires that end beside it: Reset, shift_register_1_p2, shift_register_1_p3, InstructionIn, {16{1'b0}}, shift_register_1_p6, shift_register_1_p7, QueryInstruction, shift_register_1_p9, shift_register_1_p6, shift_register_1_p7, QueryInstruction
  and and_2 (shift_register_1_p2, Stalled, InstrExec);
  or or_1 (shift_register_1_p3, IL_Flank, and_3_out);
  and and_3 (and_3_out, IE_Flank, Stalled);
  and and_4 (PC_CLK, IE_Flank, ~Stalled);  // AND_Gate
  S_R_Flip_Flop #(.trigger("high")) s_r_ff_1 (
    .S(StallRequired), .R(or_2_out), .clk(1'b1), .Q(Stalled));  // open: reset, Qn, preset
  or or_2 (or_2_out, and_1_out, Reset);
  and and_5 (IL_Flank, InstrLoad, not_1_out);
  and and_6 (IE_Flank, InstrExec, not_2_out);
  InstructionDecoder InstructionDecoder_1 (
    .Instruction(shift_register_1_p9), .Reg1(RF_Reg1), .Reg1Read(RF_Reg1_Read), .Reg2(RF_Reg2),
    .Reg2Read(RF_Reg2_Read), .USE_MA(USE_MA));  // open: WriteReg, Immediate, RF_WHB, RF_WLB, DIn_Sel, RAM_Src, RAM_Read, RAM_Write, JMP, JMP_Condintional, JMP_Relative, JMP_ConditionalMode, IsALUOP, IsRAMOP, IsEXTOP
  InstructionDecoder InstructionDecoder_2 (
    .Instruction(shift_register_1_p6), .WriteReg(Exc_WriteAddr), .RF_WHB(InstructionDecoder_2_rf_whb),
    .RF_WLB(InstructionDecoder_2_rf_wlb), .JMP(StallRequired), .IsALUOP(Exc_ALU));  // open: Reg1, Reg1Read, Reg2, Reg2Read, Immediate, DIn_Sel, RAM_Src, RAM_Read, RAM_Write, USE_MA, JMP_Condintional, JMP_Relative, JMP_ConditionalMode, IsRAMOP, IsEXTOP
  or or_3 (or_3_out, InstructionDecoder_2_rf_whb, InstructionDecoder_2_rf_wlb);
  or or_4 (Exc_Write, or_3_out, Exc_ALU);
  InstructionDecoder InstructionDecoder_3 (.Instruction(shift_register_1_p7));  // open: Reg1, Reg1Read, Reg2, Reg2Read, WriteReg, Immediate, RF_WHB, RF_WLB, DIn_Sel, RAM_Src, RAM_Read, RAM_Write, USE_MA, JMP, JMP_Condintional, JMP_Relative, JMP_ConditionalMode, IsALUOP, IsRAMOP, IsEXTOP
  Comparator #(.mode("unsigned"), .width(4)) comparator_1 (
    .a(RF_Reg1), .b(4'b1111), .eq(comparator_1_eq));  // open: gt, lt
  Comparator #(.mode("unsigned"), .width(4)) comparator_2 (
    .a(RF_Reg2), .b(4'b1111), .eq(comparator_2_eq));  // open: gt, lt
  Comparator #(.mode("unsigned"), .width(4)) comparator_3 (
    .a(RF_Reg1), .b(Exc_WriteAddr), .eq(comparator_3_eq));  // open: gt, lt
  Comparator #(.mode("unsigned"), .width(4)) comparator_4 (
    .a(RF_Reg2), .b(Exc_WriteAddr), .eq(comparator_4_eq));  // open: gt, lt
  and and_7 (Reg1_ReadsFlags, RF_Reg1_Read, comparator_1_eq);
  and and_8 (Reg2_ReadsFlags, comparator_2_eq, RF_Reg2_Read);
  and and_9 (Reg1_ReadsExcResults, RF_Reg1_Read, comparator_3_eq);
  and and_10 (Reg2_ReadsExcResults, comparator_4_eq, RF_Reg2_Read);
  Comparator #(.mode("unsigned"), .width(4)) comparator_5 (
    .a(Exc_WriteAddr), .b(4'b1010), .eq(comparator_5_eq));  // open: gt, lt
  and and_11 (MA_ReadsExcResults, USE_MA, comparator_5_eq);
  and and_12 (and_12_out, Exc_Write, Reg1_ReadsExcResults);
  and and_13 (and_13_out, Exc_ALU, Reg1_ReadsFlags);
  and and_14 (and_14_out, Exc_Write, Reg2_ReadsExcResults);
  and and_15 (and_15_out, Exc_ALU, Reg2_ReadsFlags);
  Priority_Encoder #(.select(2)) priority_encoder_1 (
    .in1(1'b1), .in2(and_12_out), .in3(and_13_out), .out(priority_encoder_1_out));  // open: in0, gs, en_out, en_in
  Priority_Encoder #(.select(2)) priority_encoder_2 (
    .in1(1'b1), .in2(and_14_out), .in3(and_15_out), .out(priority_encoder_2_out));  // open: in0, gs, en_out, en_in
  Priority_Encoder #(.select(1)) priority_encoder_3 (
    .in0(1'b1), .in1(MA_ReadsExcResults), .out(priority_encoder_3_out[4]));  // open: gs, en_out, en_in
  // Shift_Register #(.length(4), .width(5)) shift_register_2: pin names not known; wires that end beside it: Reset, InstrExec, {priority_encoder_3_out[4], priority_encoder_2_out, priority_encoder_1_out}, InstructionForwarding

  // Notes on the sheet:
  //   Delete RF Read Instruction and PC:=PC-1
  //   RF Read
  //   Execute
  //   Writeback
  //   Combine with ALU/Write Checks
  //   Pipeline Forwarding Memory
endmodule

module JumpController (
  input  JMP,
  input  JMP_Condintional,
  input  JMP_Relative,
  input  [2:0] JMP_ConditionalMode,
  input  [15:0] Flags,
  input  [15:0] JumpAddress,
  input  [15:0] PC_In,
  output PC_DIn,
  output [15:0] PC_Out
);

  wire ALUFlagUnpacker_1_biggerzero, ALUFlagUnpacker_1_boolflag, ALUFlagUnpacker_1_carryflag,
       ALUFlagUnpacker_1_overflow, ALUFlagUnpacker_1_smallerzero, ALUFlagUnpacker_1_zeroflag,
       JumpConditionFullfilled, or_1_out;
  wire [15:0] adder_1_out, subtractor_1_out;

  ALUFlagUnpacker ALUFlagUnpacker_1 (
    .PackedFlags(Flags), .CarryFlag(ALUFlagUnpacker_1_carryflag), .ZeroFlag(ALUFlagUnpacker_1_zeroflag),
    .SmallerZero(ALUFlagUnpacker_1_smallerzero), .BiggerZero(ALUFlagUnpacker_1_biggerzero),
    .Overflow(ALUFlagUnpacker_1_overflow), .BoolFlag(ALUFlagUnpacker_1_boolflag));
  Multiplexer #(.select(3)) multiplexer_1 (
    .in0(ALUFlagUnpacker_1_carryflag), .in1(ALUFlagUnpacker_1_zeroflag), .in2(ALUFlagUnpacker_1_smallerzero),
    .in3(ALUFlagUnpacker_1_biggerzero), .in4(ALUFlagUnpacker_1_overflow), .in5(ALUFlagUnpacker_1_boolflag),
    .in6(1'b0), .in7(1'b0), .out(JumpConditionFullfilled), .sel(JMP_ConditionalMode));
  Adder #(.width(16)) adder_1 (.a(JumpAddress), .b(PC_In), .out(adder_1_out));  // open: cin, cout
  Subtractor #(.width(16)) subtractor_1 (.a(adder_1_out), .b(16'h1), .out(subtractor_1_out));  // open: bin, bout
  or or_1 (or_1_out, ~JMP_Condintional, JumpConditionFullfilled);  // OR_Gate
  Multiplexer #(.width(16)) multiplexer_2 (.in0(JumpAddress), .in1(subtractor_1_out), .out(PC_Out), .sel(JMP_Relative));
  and and_1 (PC_DIn, JMP, or_1_out);
endmodule

module WriteBackPipelineStage (
  input  InstrLoad,
  input  Reset,
  input  [3:0] WriteAddress,
  input  [15:0] WriteData,
  input  [15:0] Flags,
  input  WHB,
  input  WLB,
  input  Is_ALUOP,
  input  JMP,
  output [3:0] WriteAddress_out,
  output [15:0] WriteData_out,
  output [15:0] Flags_out,
  output WHB_out,
  output WLB_out,
  output IS_ALUOP_out,
  output JMP_out
);

  Register #(.width(4)) register_1 (.D(WriteAddress), .clk(InstrLoad), .Q(WriteAddress_out), .clr(Reset));  // open: en
  Register #(.width(16)) register_2 (.D(WriteData), .clk(InstrLoad), .Q(WriteData_out), .clr(Reset));  // open: en
  Register #(.width(16)) register_3 (.D(Flags), .clk(InstrLoad), .Q(Flags_out), .clr(Reset));  // open: en
  Register #(.width(1)) register_4 (.D(WHB), .clk(InstrLoad), .Q(WHB_out), .clr(Reset));  // open: en
  Register #(.width(1)) register_5 (.D(WLB), .clk(InstrLoad), .Q(WLB_out), .clr(Reset));  // open: en
  Register #(.width(1)) register_6 (.D(Is_ALUOP), .clk(InstrLoad), .Q(IS_ALUOP_out), .clr(Reset));  // open: en
  Register #(.width(1)) register_7 (.D(JMP), .clk(InstrLoad), .Q(JMP_out), .clr(Reset));  // open: en
endmodule

module ExecutePipelineStage (
  input  InstrLoad,
  input  Reset,
  input  [15:0] Operand1,
  input  [15:0] Operand2,
  input  [15:0] Immediate,
  input  [15:0] MA,
  input  [3:0] WriteAddress,
  input  WHB,
  input  WLB,
  input  [1:0] DIn_SEL,
  input  RAM_Src,
  input  RAM_Read,
  input  RAM_Write,
  input  Use_MA,
  input  JMP,
  input  JMP_Conditional,
  input  JMP_Relative,
  input  [2:0] JMP_Condition,
  input  Is_ALUOP,
  input  Is_RAMOP,
  input  Is_EXTOP,
  output [15:0] Operand1_out,
  output [15:0] Operand2_out,
  output [15:0] Immediate_out,
  output [15:0] MA_out,
  output [3:0] WriteAddress_out,
  output WHB_out,
  output WLB_out,
  output [1:0] DIn_SEL_out,
  output RAM_Src_out,
  output RAM_Read_out,
  output RAM_Write_out,
  output Use_MA_out,
  output JMP_out,
  output JMP_Condintional_out,
  output JMP_Relative_out,
  output [2:0] JMP_Condition_out,
  output IS_ALUOP_out,
  output Is_RAMOP_out,
  output Is_EXTOP_out
);

  Register #(.width(16)) register_1 (.D(Operand1), .clk(InstrLoad), .Q(Operand1_out), .clr(Reset));  // open: en
  Register #(.width(16)) register_2 (.D(Operand2), .clk(InstrLoad), .Q(Operand2_out), .clr(Reset));  // open: en
  Register #(.width(16)) register_3 (.D(Immediate), .clk(InstrLoad), .Q(Immediate_out), .clr(Reset));  // open: en
  Register #(.width(16)) register_4 (.D(MA), .clk(InstrLoad), .Q(MA_out), .clr(Reset));  // open: en
  Register #(.width(4)) register_5 (.D(WriteAddress), .clk(InstrLoad), .Q(WriteAddress_out), .clr(Reset));  // open: en
  Register #(.width(1)) register_6 (.D(WHB), .clk(InstrLoad), .Q(WHB_out), .clr(Reset));  // open: en
  Register #(.width(1)) register_7 (.D(WLB), .clk(InstrLoad), .Q(WLB_out), .clr(Reset));  // open: en
  Register #(.width(2)) register_8 (.D(DIn_SEL), .clk(InstrLoad), .Q(DIn_SEL_out), .clr(Reset));  // open: en
  Register #(.width(1)) register_9 (.D(RAM_Src), .clk(InstrLoad), .Q(RAM_Src_out), .clr(Reset));  // open: en
  Register #(.width(1)) register_10 (.D(RAM_Read), .clk(InstrLoad), .Q(RAM_Read_out), .clr(Reset));  // open: en
  Register #(.width(1)) register_11 (.D(RAM_Write), .clk(InstrLoad), .Q(RAM_Write_out), .clr(Reset));  // open: en
  Register #(.width(1)) register_12 (.D(Use_MA), .clk(InstrLoad), .Q(Use_MA_out), .clr(Reset));  // open: en
  Register #(.width(1)) register_13 (.D(JMP), .clk(InstrLoad), .Q(JMP_out), .clr(Reset));  // open: en
  Register #(.width(1)) register_14 (
    .D(JMP_Conditional), .clk(InstrLoad), .Q(JMP_Condintional_out), .clr(Reset));  // open: en
  Register #(.width(1)) register_15 (.D(JMP_Relative), .clk(InstrLoad), .Q(JMP_Relative_out), .clr(Reset));  // open: en
  Register #(.width(3)) register_16 (
    .D(JMP_Condition), .clk(InstrLoad), .Q(JMP_Condition_out), .clr(Reset));  // open: en
  Register #(.width(1)) register_17 (.D(Is_ALUOP), .clk(InstrLoad), .Q(IS_ALUOP_out), .clr(Reset));  // open: en
  Register #(.width(1)) register_18 (.D(Is_RAMOP), .clk(InstrLoad), .Q(Is_RAMOP_out), .clr(Reset));  // open: en
  Register #(.width(1)) register_19 (.D(Is_EXTOP), .clk(InstrLoad), .Q(Is_EXTOP_out), .clr(Reset));  // open: en
endmodule

module VGAController (
  input  [15:0] EXT0_A0,
  input  [15:0] EXT0_A1,
  input  EXT0_CLK,
  output [7:0] PixX,
  output [7:0] PixY,
  output [23:0] RGB,
  output CLK_Out
);


  assign CLK_Out = EXT0_CLK;
  assign PixX = EXT0_A0[7:0];
  assign PixY = EXT0_A0[15:8];
  assign RGB = {EXT0_A1[11:8], 4'b0000, EXT0_A1[7:4], 4'b0000, EXT0_A1[3:0], 4'b0000};
endmodule

module IM_Modifier (
  input  [15:0] Reg1_Read,
  input  [15:0] Immediate,
  input  IMH,
  input  IML,
  output [15:0] Union
);

  Multiplexer #(.select(2), .width(16)) multiplexer_1 (
    .in0(Reg1_Read), .in1({Immediate[7:0], Reg1_Read[7:0]}), .in2({Reg1_Read[15:8], Immediate[7:0]}),
    .in3(Immediate), .out(Union), .sel({IML, IMH}));
endmodule

module Banker (
  input  [15:0] BankID,
  input  [15:0] DataIn,
  input  [15:0] Address,
  input  WE,
  input  OE,
  input  CLK,
  output [15:0] DataOut
);

  wire and_1_out, and_2_out, and_3_out, and_4_out, and_5_out, and_6_out, and_7_out, and_8_out, and_9_out,
       decoder_1_out0, decoder_1_out1, decoder_1_out2;
  wire [3:0] bit_extender_1_out;
  wire [15:0] ram_1_dout, ram_2_dout, ram_3_dout;

  Bit_Extender #(.in_width(16), .out_width(4)) bit_extender_1 (.in(BankID), .out(bit_extender_1_out));
  Decoder #(.enable("false"), .select(4)) decoder_1 (
    .out0(decoder_1_out0), .out1(decoder_1_out1), .out2(decoder_1_out2), .sel(bit_extender_1_out));  // open: out3, out4, out5, out6, out7, out8, out9, out10, out11, out12, out13, out14, out15
  RAM #(.addrWidth(16), .dataWidth(16)) ram_1 (
    .addr(Address), .we(and_1_out), .oe(and_2_out), .clk(and_3_out), .din(DataIn), .dout(ram_1_dout));
  and and_1 (and_1_out, WE, decoder_1_out0);
  and and_2 (and_2_out, OE, decoder_1_out0);
  and and_3 (and_3_out, CLK, decoder_1_out0);
  RAM #(.addrWidth(16), .dataWidth(16)) ram_2 (
    .addr(Address), .we(and_4_out), .oe(and_5_out), .clk(and_6_out), .din(DataIn), .dout(ram_2_dout));
  and and_4 (and_4_out, WE, decoder_1_out1);
  and and_5 (and_5_out, OE, decoder_1_out1);
  and and_6 (and_6_out, CLK, decoder_1_out1);
  RAM #(.addrWidth(16), .dataWidth(16)) ram_3 (
    .addr(Address), .we(and_7_out), .oe(and_8_out), .clk(and_9_out), .din(DataIn), .dout(ram_3_dout));
  and and_7 (and_7_out, WE, decoder_1_out2);
  and and_8 (and_8_out, OE, decoder_1_out2);
  and and_9 (and_9_out, CLK, decoder_1_out2);
  Multiplexer #(.select(4), .width(16)) multiplexer_1 (
    .in0(ram_1_dout), .in1(ram_2_dout), .in2(ram_3_dout), .out(DataOut), .sel(bit_extender_1_out));  // open: in3, in4, in5, in6, in7, in8, in9, in10, in11, in12, in13, in14, in15
endmodule
