// Logisim project DesignVorschlag1.circ as structural Verilog: 13 circuits, main circuit main
module main (
);

  wire alu_1_boolflag, alu_1_carryflag, alu_1_zeroflag, ALU_BoolFlag, ALU_CarryFlag, ALU_ZeroFlag,
       button_1_out, button_2_out, clock_1_out, clockcontroller_1_instrload,
       externaldevicecontroller_1_ext0_clk, externaldevicecontroller_1_ext0_en,
       externaldevicecontroller_1_ext1_clk, externaldevicecontroller_1_ext1_en, InstrExec, InstrSave,
       instructiondecoder_1_isaluop, instructiondecoder_1_isextop, instructiondecoder_1_jmp,
       instructiondecoder_1_jmp_condintional, instructiondecoder_1_jmp_relative,
       instructiondecoder_1_ram_read, instructiondecoder_1_ram_src, instructiondecoder_1_ram_write,
       instructiondecoder_1_rf_whb, instructiondecoder_1_rf_wlb, instructiondecoder_1_use_ma,
       jumpcontroller_1_pc_din, vgacontroller_1_clk_out;
  wire [1:0] instructiondecoder_1_din_sel, instructiondecoder_1_jmp_conditionalmode;
  wire [3:0] alu_1_alu_output, alu_1_alu_output_2, alu_1_alu_output_3, alu_1_alu_output_4,
       bit_extender_1_out, bit_extender_2_out, instructiondecoder_1_reg1, instructiondecoder_1_reg2,
       instructiondecoder_1_writereg;
  wire [7:0] vgacontroller_1_pixx, vgacontroller_1_pixy;
  wire [15:0] adder_1_out, counter_1_q, externaldevicecontroller_1_ext0_a0,
       externaldevicecontroller_1_ext0_a1, externaldevicecontroller_1_ext1_a0,
       externaldevicecontroller_1_ext1_a1, flagpacker_1_packedflags, instructiondecoder_1_immediate,
       jumpcontroller_1_pc_out, multiplexer_1_out, multiplexer_2_out, multiplexer_3_out, R1, R2, ram_1_dout,
       regfile_1_lastaluflags, regfile_1_ma, rom_1_data;
  wire [23:0] vgacontroller_1_rgb;

  Clock clock_1 (.out(clock_1_out));
  Button button_1 (.out(button_1_out));
  ROM #(.addrWidth(16), .dataWidth(16)) rom_1 (.addr(counter_1_q), .data(rom_1_data));
  Counter #(.max('hffff), .width(16)) counter_1 (
    .load(jumpcontroller_1_pc_din), .D(jumpcontroller_1_pc_out), .Q(counter_1_q),
    .clk(clockcontroller_1_instrload), .clr(button_1_out));  // open: count, carry, up
  ClockController clockcontroller_1 (
    .RawCLK(clock_1_out), .Reset(button_1_out), .InstrLoad(clockcontroller_1_instrload),
    .InstrExec(InstrExec), .InstrSave(InstrSave));
  JumpController jumpcontroller_1 (
    .JMP(instructiondecoder_1_jmp), .JMP_Condintional(instructiondecoder_1_jmp_condintional),
    .JMP_Relative(instructiondecoder_1_jmp_relative),
    .JMP_ConditionalMode(instructiondecoder_1_jmp_conditionalmode), .CarryFlag(ALU_CarryFlag),
    .ZeroFlag(ALU_ZeroFlag), .BoolFlag(ALU_BoolFlag), .JumpAddress(instructiondecoder_1_immediate),
    .PC_In(counter_1_q), .PC_DIn(jumpcontroller_1_pc_din), .PC_Out(jumpcontroller_1_pc_out));
  InstructionDecoder instructiondecoder_1 (
    .Instruction(rom_1_data), .Reg1(instructiondecoder_1_reg1), .Reg2(instructiondecoder_1_reg2),
    .WriteReg(instructiondecoder_1_writereg), .Immediate(instructiondecoder_1_immediate),
    .RF_WLB(instructiondecoder_1_rf_wlb), .RF_WHB(instructiondecoder_1_rf_whb),
    .DIn_Sel(instructiondecoder_1_din_sel), .RAM_Src(instructiondecoder_1_ram_src),
    .RAM_Read(instructiondecoder_1_ram_read), .RAM_Write(instructiondecoder_1_ram_write),
    .USE_MA(instructiondecoder_1_use_ma), .JMP(instructiondecoder_1_jmp),
    .JMP_Condintional(instructiondecoder_1_jmp_condintional),
    .JMP_Relative(instructiondecoder_1_jmp_relative),
    .JMP_ConditionalMode(instructiondecoder_1_jmp_conditionalmode), .IsALUOP(instructiondecoder_1_isaluop),
    .IsEXTOP(instructiondecoder_1_isextop));
  Multiplexer #(.select(2), .width(16)) multiplexer_1 (
    .in0(ram_1_dout), .in1(instructiondecoder_1_immediate), .in2(R1), .out(multiplexer_1_out),
    .sel(instructiondecoder_1_din_sel));  // open: in3
  Bit_Extender #(.in_width(16), .out_width(4)) bit_extender_1 (
    .in(instructiondecoder_1_immediate), .out(bit_extender_1_out));
  FlagUnpacker flagunpacker_1 (
    .PackedFlags(regfile_1_lastaluflags), .CarryFlag(ALU_CarryFlag), .ZeroFlag(ALU_ZeroFlag),
    .BoolFlag(ALU_BoolFlag));
  RegFile regfile_1 (
    .WriteData(multiplexer_1_out), .WHB(instructiondecoder_1_rf_whb), .WLB(instructiondecoder_1_rf_wlb),
    .CLK(InstrSave), .ReadAddress1(instructiondecoder_1_reg1), .ReadAddress2(instructiondecoder_1_reg2),
    .WriteAddress(instructiondecoder_1_writereg),
    .ALU_Output({alu_1_alu_output_4, alu_1_alu_output_3, alu_1_alu_output_2, alu_1_alu_output}),
    .Flags(flagpacker_1_packedflags), .IsALUOP(instructiondecoder_1_isaluop), .Operand1(R1), .Operand2(R2),
    .MA(regfile_1_ma), .LastALUFlags(regfile_1_lastaluflags));
  Multiplexer #(.width(16)) multiplexer_2 (
    .in0(R2), .in1(instructiondecoder_1_immediate), .out(multiplexer_2_out),
    .sel(instructiondecoder_1_ram_src));
  Adder #(.width(16)) adder_1 (.a(regfile_1_ma), .b(multiplexer_2_out), .out(adder_1_out));  // open: cin, cout
  Bit_Extender #(.in_width(16), .out_width(4)) bit_extender_2 (
    .in(instructiondecoder_1_immediate), .out(bit_extender_2_out));
  Hex_Digit_Display hex_digit_display_1 (.value(alu_1_alu_output_4));  // open: dp
  ALU alu_1 (
    .ALU_Function(bit_extender_1_out), .Operand1(R1), .Operand2(R2),
    .ALU_Output({alu_1_alu_output_4, alu_1_alu_output_3, alu_1_alu_output_2, alu_1_alu_output}),
    .CarryFlag(alu_1_carryflag), .ZeroFlag(alu_1_zeroflag), .BoolFlag(alu_1_boolflag));
  Multiplexer #(.width(16)) multiplexer_3 (
    .in0(multiplexer_2_out), .in1(adder_1_out), .out(multiplexer_3_out), .sel(instructiondecoder_1_use_ma));
  Hex_Digit_Display hex_digit_display_2 (.value(alu_1_alu_output_3));  // open: dp
  Hex_Digit_Display hex_digit_display_3 (.value(alu_1_alu_output_2));  // open: dp
  Hex_Digit_Display hex_digit_display_4 (.value(alu_1_alu_output));  // open: dp
  RAM #(.addrWidth(16), .dataWidth(16)) ram_1 (
    .addr(multiplexer_3_out), .we(instructiondecoder_1_ram_write), .oe(instructiondecoder_1_ram_read),
    .clk(InstrExec), .din(R1), .dout(ram_1_dout));
  ExternalDeviceController externaldevicecontroller_1 (
    .ControlExternalDevice(instructiondecoder_1_isextop), .ExternalDeviceID(bit_extender_2_out),
    .ExternalArgument1(R1), .ExternalArgument2(R2), .CLK(InstrExec),
    .EXT0_EN(externaldevicecontroller_1_ext0_en), .EXT0_A0(externaldevicecontroller_1_ext0_a0),
    .EXT0_A1(externaldevicecontroller_1_ext0_a1), .EXT0_CLK(externaldevicecontroller_1_ext0_clk),
    .EXT1_EN(externaldevicecontroller_1_ext1_en), .EXT1_A0(externaldevicecontroller_1_ext1_a0),
    .EXT1_A1(externaldevicecontroller_1_ext1_a1), .EXT1_CLK(externaldevicecontroller_1_ext1_clk));  // open: EXT2_EN, EXT2_A0, EXT2_A1, EXT2_CLK, EXT3_EN, EXT3_A0, EXT3_A1, EXT3_CLK
  FlagPacker flagpacker_1 (
    .CarryFlag(alu_1_carryflag), .ZeroFlag(alu_1_zeroflag), .BoolFlag(alu_1_boolflag),
    .PackedFlags(flagpacker_1_packedflags));
  NumberDisplay numberdisplay_1 (
    .EXT0_EN(externaldevicecontroller_1_ext0_en), .EXT0_A0(externaldevicecontroller_1_ext0_a0),
    .EXT0_A1(externaldevicecontroller_1_ext0_a1), .EXT0_CLK(externaldevicecontroller_1_ext0_clk));
  VGAController vgacontroller_1 (
    .EXT0_EN(externaldevicecontroller_1_ext1_en), .EXT0_A0(externaldevicecontroller_1_ext1_a0),
    .EXT0_A1(externaldevicecontroller_1_ext1_a1), .EXT0_CLK(externaldevicecontroller_1_ext1_clk),
    .PixX(vgacontroller_1_pixx), .PixY(vgacontroller_1_pixy), .RGB(vgacontroller_1_rgb),
    .CLK_Out(vgacontroller_1_clk_out));
  Button button_2 (.out(button_2_out));
  // RGB_Video #(.cursor("No Cursor"), .height(256), .width(256)) rgb_video_1: pin names not known; wires that end beside it: button_2_out, vgacontroller_1_clk_out, 1'b1, vgacontroller_1_pixx, vgacontroller_1_pixy, vgacontroller_1_rgb

  // Notes on the sheet:
  //   contents of rom_1 (hex, n*v repeats v):
  //   4000 5000 1000 49ff 590f 4001 5000 10e0 f1e9 a006
endmodule

module RegFile (
  input  [15:0] WriteData,
  input  WHB,
  input  WLB,
  input  CLK,
  input  [3:0] ReadAddress1,
  input  [3:0] ReadAddress2,
  input  [3:0] WriteAddress,
  input  [15:0] ALU_Output,
  input  [15:0] Flags,
  input  IsALUOP,
  output [15:0] Operand1,
  output [15:0] Operand2,
  output [15:0] MA,
  output [15:0] LastALUFlags
);

  wire and_1_out, decoder_1_out0, decoder_1_out1, decoder_1_out2, decoder_1_out3, decoder_1_out4,
       decoder_1_out5, decoder_1_out6, decoder_1_out7, decoder_1_out8, decoder_1_out9, decoder_1_out10,
       decoder_1_out11, decoder_1_out12, decoder_1_out13, or_1_out;
  wire [7:0] multiplexer_1_out, multiplexer_2_out, multiplexer_3_out;
  wire [15:0] register_1_q, register_2_q, register_3_q, register_4_q, register_5_q, register_6_q,
       register_7_q, register_8_q, register_9_q, register_10_q, register_12_q, register_13_q, register_14_q,
       register_15_q, WriteRegisterValue;

  Decoder #(.select(4)) decoder_1 (
    .out0(decoder_1_out0), .out1(decoder_1_out1), .out2(decoder_1_out2), .out3(decoder_1_out3),
    .out4(decoder_1_out4), .out5(decoder_1_out5), .out6(decoder_1_out6), .out7(decoder_1_out7),
    .out8(decoder_1_out8), .out9(decoder_1_out9), .out10(decoder_1_out10), .out11(decoder_1_out11),
    .out12(decoder_1_out12), .out13(decoder_1_out13), .sel(WriteAddress));  // open: out14, out15, en
  Multiplexer #(.width(8)) multiplexer_1 (
    .in0(WriteData[7:0]), .in1(WriteData[15:8]), .out(multiplexer_1_out), .sel(WLB));
  or or_1 (or_1_out, WHB, WLB);
  Multiplexer #(.width(8)) multiplexer_2 (
    .in0(WriteRegisterValue[15:8]), .in1(multiplexer_1_out), .out(multiplexer_2_out), .sel(WHB));
  Multiplexer #(.width(8)) multiplexer_3 (
    .in0(WriteRegisterValue[7:0]), .in1(WriteData[7:0]), .out(multiplexer_3_out), .sel(WLB));
  and and_1 (and_1_out, or_1_out, CLK);
  Register #(.width(16)) register_1 (
    .D({multiplexer_2_out, multiplexer_3_out}), .en(decoder_1_out0), .Q(register_1_q), .clk(and_1_out));  // open: clr
  Register #(.width(16)) register_2 (
    .D({multiplexer_2_out, multiplexer_3_out}), .en(decoder_1_out1), .Q(register_2_q), .clk(and_1_out));  // open: clr
  Register #(.width(16)) register_3 (
    .D({multiplexer_2_out, multiplexer_3_out}), .en(decoder_1_out2), .Q(register_3_q), .clk(and_1_out));  // open: clr
  Register #(.width(16)) register_4 (
    .D({multiplexer_2_out, multiplexer_3_out}), .en(decoder_1_out3), .Q(register_4_q), .clk(and_1_out));  // open: clr
  Register #(.width(16)) register_5 (
    .D({multiplexer_2_out, multiplexer_3_out}), .en(decoder_1_out4), .Q(register_5_q), .clk(and_1_out));  // open: clr
  Register #(.width(16)) register_6 (
    .D({multiplexer_2_out, multiplexer_3_out}), .en(decoder_1_out5), .Q(register_6_q), .clk(and_1_out));  // open: clr
  Register #(.width(16)) register_7 (
    .D({multiplexer_2_out, multiplexer_3_out}), .en(decoder_1_out6), .Q(register_7_q), .clk(and_1_out));  // open: clr
  Register #(.width(16)) register_8 (
    .D({multiplexer_2_out, multiplexer_3_out}), .en(decoder_1_out7), .Q(register_8_q), .clk(and_1_out));  // open: clr
  Register #(.width(16)) register_9 (
    .D({multiplexer_2_out, multiplexer_3_out}), .en(decoder_1_out8), .Q(register_9_q), .clk(and_1_out));  // open: clr
  Register #(.width(16)) register_10 (
    .D({multiplexer_2_out, multiplexer_3_out}), .en(decoder_1_out9), .Q(register_10_q), .clk(and_1_out));  // open: clr
  Register #(.width(16)) register_11 (
    .D({multiplexer_2_out, multiplexer_3_out}), .en(decoder_1_out10), .Q(MA), .clk(and_1_out));  // open: clr
  Register #(.width(16)) register_12 (
    .D({multiplexer_2_out, multiplexer_3_out}), .en(decoder_1_out11), .Q(register_12_q), .clk(and_1_out));  // open: clr
  Register #(.width(16)) register_13 (
    .D({multiplexer_2_out, multiplexer_3_out}), .en(decoder_1_out12), .Q(register_13_q), .clk(and_1_out));  // open: clr
  Register #(.width(16)) register_14 (
    .D({multiplexer_2_out, multiplexer_3_out}), .en(decoder_1_out13), .Q(register_14_q), .clk(and_1_out));  // open: clr
  Register #(.width(16)) register_15 (.D(ALU_Output), .en(IsALUOP), .Q(register_15_q), .clk(CLK));  // open: clr
  Register #(.width(16)) register_16 (.D(Flags), .en(IsALUOP), .Q(LastALUFlags), .clk(CLK));  // open: clr
  Multiplexer #(.select(4), .width(16)) multiplexer_4 (
    .in0(register_1_q), .in1(register_2_q), .in2(register_3_q), .in3(register_4_q), .in4(register_5_q),
    .in5(register_6_q), .in6(register_7_q), .in7(register_8_q), .in8(register_9_q), .in9(register_10_q),
    .in10(MA), .in11(register_12_q), .in12(register_13_q), .in13(register_14_q), .in14(register_15_q),
    .in15(LastALUFlags), .out(WriteRegisterValue), .sel(WriteAddress));
  Multiplexer #(.select(4), .width(16)) multiplexer_5 (
    .in0(register_1_q), .in1(register_2_q), .in2(register_3_q), .in3(register_4_q), .in4(register_5_q),
    .in5(register_6_q), .in6(register_7_q), .in7(register_8_q), .in8(register_9_q), .in9(register_10_q),
    .in10(MA), .in11(register_12_q), .in12(register_13_q), .in13(register_14_q), .in14(register_15_q),
    .in15(LastALUFlags), .out(Operand1), .sel(ReadAddress1));
  Multiplexer #(.select(4), .width(16)) multiplexer_6 (
    .in0(register_1_q), .in1(register_2_q), .in2(register_3_q), .in3(register_4_q), .in4(register_5_q),
    .in5(register_6_q), .in6(register_7_q), .in7(register_8_q), .in8(register_9_q), .in9(register_10_q),
    .in10(MA), .in11(register_12_q), .in12(register_13_q), .in13(register_14_q), .in14(register_15_q),
    .in15(LastALUFlags), .out(Operand2), .sel(ReadAddress2));

  // Other names for the same wires on the sheet: Raw_CLK = CLK
endmodule

module ALU (
  input  [3:0] ALU_Function,
  input  [15:0] Operand1,
  input  [15:0] Operand2,
  output [15:0] ALU_Output,
  output CarryFlag,
  output ZeroFlag,
  output BoolFlag
);

  wire arithmeticunit_1_carryout;
  wire [15:0] arithmeticunit_1_arithmetic_out, logicalunit_1_logicalout;

  and and_1 (CarryFlag, ~ALU_Function[3], arithmeticunit_1_carryout);  // AND_Gate
  ArithmeticUnit arithmeticunit_1 (
    .ALU_Function(ALU_Function), .Operand1(Operand1), .Operand2(Operand2),
    .Arithmetic_Out(arithmeticunit_1_arithmetic_out), .CarryOut(arithmeticunit_1_carryout));
  LogicalUnit logicalunit_1 (
    .ALU_Function(ALU_Function), .Operand1(Operand1), .Operand2(Operand2),
    .LogicalOut(logicalunit_1_logicalout));
  Multiplexer #(.width(16)) multiplexer_1 (
    .in0(arithmeticunit_1_arithmetic_out), .in1(logicalunit_1_logicalout), .out(ALU_Output),
    .sel(ALU_Function[3]));
  nor nor_1 (ZeroFlag, ALU_Output[0], ALU_Output[1], ALU_Output[2], ALU_Output[3], ALU_Output[4], ALU_Output[5], ALU_Output[6], ALU_Output[7], ALU_Output[9], ALU_Output[10], ALU_Output[11], ALU_Output[12], ALU_Output[13], ALU_Output[14], ALU_Output[15], ALU_Output[8]);

  assign BoolFlag = ALU_Output[0];
endmodule

module LogicalUnit (
  input  [3:0] ALU_Function,
  input  [15:0] Operand1,
  input  [15:0] Operand2,
  output [15:0] LogicalOut
);

  wire [15:0] and_1_out, bit_extender_1_out, multiplexer_1_out, or_1_out, xor_1_out;

  assign and_1_out = Operand1 & Operand2;  // AND_Gate and_1, 16 bits wide
  assign or_1_out = Operand1 | Operand2;  // OR_Gate or_1, 16 bits wide
  assign xor_1_out = Operand1 ^ Operand2;  // XOR_Gate xor_1, 16 bits wide
  Multiplexer #(.select(2), .width(16)) multiplexer_1 (
    .in0(Operand1), .in1(and_1_out), .in2(or_1_out), .in3(xor_1_out), .out(multiplexer_1_out),
    .sel(ALU_Function[1:0]));
  assign bit_extender_1_out = {{15{ALU_Function[2]}}, ALU_Function[2]};  // Bit_Extender bit_extender_1
  assign LogicalOut = bit_extender_1_out ^ multiplexer_1_out;  // XOR_Gate xor_2, 16 bits wide

  // Other names for the same wires on the sheet: LogicalFunction[1:0] = ALU_Function[1:0]; Inverted = ALU_Function[2]
endmodule

module ArithmeticUnit (
  input  [3:0] ALU_Function,
  input  [15:0] Operand1,
  input  [15:0] Operand2,
  output [15:0] Arithmetic_Out,
  output CarryOut
);

  wire adder_1_cout, subtractor_1_bout;
  wire [3:0] bit_extender_1_out;
  wire [15:0] adder_1_out, shifter_1_out, shifter_2_out, subtractor_1_out;

  Bit_Extender #(.in_width(16), .out_width(4)) bit_extender_1 (.in(Operand2), .out(bit_extender_1_out));
  Adder #(.width(16)) adder_1 (.a(Operand1), .b(Operand2), .out(adder_1_out), .cout(adder_1_cout));  // open: cin
  Subtractor #(.width(16)) subtractor_1 (
    .a(Operand1), .b(Operand2), .out(subtractor_1_out), .bout(subtractor_1_bout));  // open: bin
  Shifter #(.width(16)) shifter_1 (.in(Operand1), .\dist (bit_extender_1_out), .out(shifter_1_out));
  Shifter #(.shift("lr"), .width(16)) shifter_2 (.in(Operand1), .\dist (bit_extender_1_out), .out(shifter_2_out));
  Multiplexer #(.select(3), .width(16)) multiplexer_1 (
    .in0(adder_1_out), .in1(subtractor_1_out), .in2(shifter_1_out), .in3(shifter_2_out), .in4({16{1'b0}}),
    .in5({16{1'b0}}), .in6({16{1'b0}}), .in7({16{1'b0}}), .out(Arithmetic_Out), .sel(ALU_Function[2:0]));
  Multiplexer #(.select(3)) multiplexer_2 (
    .in0(adder_1_cout), .in1(subtractor_1_bout), .in2(1'b0), .in3(1'b0), .in4(1'b0), .in5(1'b0), .in6(1'b0),
    .in7(1'b0), .out(CarryOut), .sel(ALU_Function[2:0]));

  // Other names for the same wires on the sheet: MathFunction[2:0] = ALU_Function[2:0]
endmodule

module InstructionDecoder (
  input  [15:0] Instruction,
  output [3:0] Reg1,
  output [3:0] Reg2,
  output [3:0] WriteReg,
  output [15:0] Immediate,
  output RF_WLB,
  output RF_WHB,
  output [1:0] DIn_Sel,
  output RAM_Src,
  output RAM_Read,
  output RAM_Write,
  output USE_MA,
  output JMP,
  output JMP_Condintional,
  output JMP_Relative,
  output [1:0] JMP_ConditionalMode,
  output IsALUOP,
  output IsEXTOP
);

  wire comparator_1_eq, comparator_2_eq, comparator_3_eq, comparator_4_eq, comparator_5_eq, comparator_6_eq,
       comparator_9_eq, comparator_10_eq, or_3_out;
  wire [15:0] bit_extender_1_out, bit_extender_2_out, bit_extender_3_out, bit_extender_4_out,
       bit_extender_5_out, bit_extender_6_out, bit_extender_7_out;

  Comparator #(.mode("unsigned"), .width(4)) comparator_1 (
    .a(Instruction[15:12]), .b(4'b0100), .eq(comparator_1_eq));  // open: gt, lt
  Comparator #(.mode("unsigned"), .width(4)) comparator_2 (
    .a(Instruction[15:12]), .b(4'b0101), .eq(comparator_2_eq));  // open: gt, lt
  Comparator #(.mode("unsigned"), .width(4)) comparator_3 (
    .a(Instruction[15:12]), .b(4'b0010), .eq(comparator_3_eq));  // open: gt, lt
  Comparator #(.mode("unsigned"), .width(4)) comparator_4 (
    .a(Instruction[15:12]), .b(4'b0110), .eq(comparator_4_eq));  // open: gt, lt
  Comparator #(.mode("unsigned"), .width(4)) comparator_5 (
    .a(Instruction[15:12]), .b(4'b0011), .eq(comparator_5_eq));  // open: gt, lt
  Comparator #(.mode("unsigned"), .width(4)) comparator_6 (
    .a(Instruction[15:12]), .b(4'b0111), .eq(comparator_6_eq));  // open: gt, lt
  Comparator #(.mode("unsigned"), .width(4)) comparator_7 (
    .a(Instruction[15:12]), .b(4'b1110), .eq(DIn_Sel[1]));  // open: gt, lt
  Comparator #(.mode("unsigned"), .width(4)) comparator_8 (
    .a(Instruction[15:12]), .b(4'b1000), .eq(JMP_Condintional));  // open: gt, lt
  Comparator #(.mode("unsigned"), .width(4)) comparator_9 (
    .a(Instruction[15:12]), .b(4'b1001), .eq(comparator_9_eq));  // open: gt, lt
  Comparator #(.mode("unsigned"), .width(4)) comparator_10 (
    .a(Instruction[15:12]), .b(4'b1010), .eq(comparator_10_eq));  // open: gt, lt
  Comparator #(.mode("unsigned"), .width(4)) comparator_11 (
    .a(Instruction[15:12]), .b(4'b0001), .eq(IsALUOP));  // open: gt, lt
  Comparator #(.mode("unsigned"), .width(4)) comparator_12 (
    .a(Instruction[15:12]), .b(4'b1111), .eq(IsEXTOP));  // open: gt, lt
  or or_1 (RF_WLB, comparator_1_eq, comparator_3_eq, comparator_4_eq, DIn_Sel[1]);
  or or_2 (RF_WHB, comparator_2_eq, comparator_3_eq, comparator_4_eq, DIn_Sel[1]);
  or or_3 (or_3_out, comparator_2_eq, comparator_1_eq);
  or or_4 (RAM_Read, comparator_4_eq, comparator_3_eq);
  or or_5 (RAM_Src, comparator_3_eq, comparator_5_eq);
  or or_6 (RAM_Write, comparator_5_eq, comparator_6_eq);
  or or_7 (JMP, JMP_Condintional, comparator_9_eq, comparator_10_eq);
  or or_8 (JMP_Relative, JMP_Condintional, comparator_9_eq);
  and and_1 (DIn_Sel[0], or_3_out, ~DIn_Sel[1]);  // AND_Gate
  assign bit_extender_1_out = {{12{1'b0}}, Instruction[11:8]};  // Bit_Extender bit_extender_1
  assign bit_extender_2_out = {{8{1'b0}}, Instruction[7:0]};  // Bit_Extender bit_extender_2
  assign bit_extender_3_out = {{8{1'b0}}, Instruction[7:0]};  // Bit_Extender bit_extender_3
  assign bit_extender_4_out = {{6{Instruction[9]}}, Instruction[9:0]};  // Bit_Extender bit_extender_4
  assign bit_extender_5_out = {{4{Instruction[11]}}, Instruction[11:0]};  // Bit_Extender bit_extender_5
  assign bit_extender_6_out = {{4{1'b0}}, Instruction[11:0]};  // Bit_Extender bit_extender_6
  assign bit_extender_7_out = {{12{1'b0}}, Instruction[11:8]};  // Bit_Extender bit_extender_7
  Multiplexer #(.select(4), .width(4)) multiplexer_1 (
    .in1(Instruction[7:4]), .in3(Instruction[11:8]), .in7(Instruction[11:8]), .in14(Instruction[3:0]),
    .in15(Instruction[7:4]), .out(Reg1), .sel(Instruction[15:12]));  // open: in0, in2, in4, in5, in6, in8, in9, in10, in11, in12, in13
  Multiplexer #(.select(4), .width(4)) multiplexer_2 (
    .in1(Instruction[3:0]), .in6(Instruction[7:4]), .in7(Instruction[7:4]), .in15(Instruction[3:0]),
    .out(Reg2), .sel(Instruction[15:12]));  // open: in0, in2, in3, in4, in5, in8, in9, in10, in11, in12, in13, in14
  Multiplexer #(.select(4), .width(4)) multiplexer_3 (
    .in2(Instruction[11:8]), .in4(Instruction[11:8]), .in5(Instruction[11:8]), .in6(Instruction[11:8]),
    .in14(Instruction[11:8]), .out(WriteReg), .sel(Instruction[15:12]));  // open: in0, in1, in3, in7, in8, in9, in10, in11, in12, in13, in15
  Multiplexer #(.select(4), .width(16)) multiplexer_4 (
    .in1(bit_extender_1_out), .in2(bit_extender_2_out), .in3(bit_extender_2_out), .in4(bit_extender_3_out),
    .in5(bit_extender_3_out), .in8(bit_extender_4_out), .in9(bit_extender_5_out), .in10(bit_extender_6_out),
    .in15(bit_extender_7_out), .out(Immediate), .sel(Instruction[15:12]));  // open: in0, in6, in7, in11, in12, in13, in14

  assign JMP_ConditionalMode = Instruction[11:10];
  assign USE_MA = Instruction[0];

  // Other names for the same wires on the sheet: RawInstr[15:0] = Instruction;
  //   InstructionName[3:0] = Instruction[15:12]
endmodule

module JumpController (
  input  JMP,
  input  JMP_Condintional,
  input  JMP_Relative,
  input  [1:0] JMP_ConditionalMode,
  input  CarryFlag,
  input  ZeroFlag,
  input  BoolFlag,
  input  [15:0] JumpAddress,
  input  [15:0] PC_In,
  output PC_DIn,
  output [15:0] PC_Out
);

  wire JumpConditionFullfilled, not_1_out, or_1_out;
  wire [15:0] adder_1_out;

  not not_1 (not_1_out, ZeroFlag);
  Multiplexer #(.select(2)) multiplexer_1 (
    .in0(CarryFlag), .in1(ZeroFlag), .in2(not_1_out), .in3(BoolFlag), .out(JumpConditionFullfilled),
    .sel(JMP_ConditionalMode));
  Adder #(.width(16)) adder_1 (.a(JumpAddress), .b(PC_In), .out(adder_1_out));  // open: cin, cout
  Multiplexer #(.width(16)) multiplexer_2 (.in0(JumpAddress), .in1(adder_1_out), .out(PC_Out), .sel(JMP_Relative));
  or or_1 (or_1_out, ~JMP_Condintional, JumpConditionFullfilled);  // OR_Gate
  and and_1 (PC_DIn, JMP, or_1_out);
endmodule

module FlagPacker (
  input  CarryFlag,
  input  ZeroFlag,
  input  BoolFlag,
  output [15:0] PackedFlags
);


  assign PackedFlags = {{13{1'b0}}, BoolFlag, ZeroFlag, CarryFlag};
endmodule

module FlagUnpacker (
  input  [15:0] PackedFlags,
  output CarryFlag,
  output ZeroFlag,
  output BoolFlag
);


  assign BoolFlag = PackedFlags[2];
  assign CarryFlag = PackedFlags[0];
  assign ZeroFlag = PackedFlags[1];
endmodule

module ExternalDeviceController (
  input  ControlExternalDevice,
  input  [3:0] ExternalDeviceID,
  input  [15:0] ExternalArgument1,
  input  [15:0] ExternalArgument2,
  input  CLK,
  output EXT0_EN,
  output [15:0] EXT0_A0,
  output [15:0] EXT0_A1,
  output EXT0_CLK,
  output EXT1_EN,
  output [15:0] EXT1_A0,
  output [15:0] EXT1_A1,
  output EXT1_CLK,
  output EXT2_EN,
  output [15:0] EXT2_A0,
  output [15:0] EXT2_A1,
  output EXT2_CLK,
  output EXT3_EN,
  output [15:0] EXT3_A0,
  output [15:0] EXT3_A1,
  output EXT3_CLK
);

  Decoder #(.select(4)) decoder_1 (
    .out0(EXT0_EN), .out1(EXT1_EN), .out2(EXT2_EN), .out3(EXT3_EN), .sel(ExternalDeviceID),
    .en(ControlExternalDevice));  // open: out4, out5, out6, out7, out8, out9, out10, out11, out12, out13, out14, out15
  and and_1 (EXT0_CLK, EXT0_EN, CLK);
  and and_2 (EXT1_CLK, EXT1_EN, CLK);
  and and_3 (EXT2_CLK, EXT2_EN, CLK);
  and and_4 (EXT3_CLK, EXT3_EN, CLK);

  assign EXT0_A0 = ExternalArgument1;
  assign EXT0_A1 = ExternalArgument2;
  assign EXT1_A0 = ExternalArgument1;
  assign EXT1_A1 = ExternalArgument2;
  assign EXT2_A0 = ExternalArgument1;
  assign EXT2_A1 = ExternalArgument2;
  assign EXT3_A0 = ExternalArgument1;
  assign EXT3_A1 = ExternalArgument2;

  // Other names for the same wires on the sheet: EA1[15:0] = ExternalArgument1; EA2[15:0] = ExternalArgument2
endmodule

module NumberDisplay (
  input  EXT0_EN,
  input  [15:0] EXT0_A0,
  input  [15:0] EXT0_A1,
  input  EXT0_CLK
);

  wire [15:0] register_1_q;
  wire [20:0] rom_1_data;

  Register #(.width(16)) register_1 (.D(EXT0_A0), .clk(EXT0_CLK), .Q(register_1_q));  // open: en, clr
  ROM #(.addrWidth(16), .dataWidth(21)) rom_1 (.addr(register_1_q), .data(rom_1_data));
  _7_Segment_Display u_7_segment_display_1 (.g(rom_1_data[20]));  // open: f, a, b, e, d, c, dp
  Hex_Digit_Display hex_digit_display_1 (.value(rom_1_data[15:12]));  // open: dp
  Hex_Digit_Display hex_digit_display_2 (.value(rom_1_data[19:16]));  // open: dp
  Hex_Digit_Display hex_digit_display_3 (.value(rom_1_data[11:8]));  // open: dp
  Hex_Digit_Display hex_digit_display_4 (.value(rom_1_data[7:4]));  // open: dp
  Hex_Digit_Display hex_digit_display_5 (.value(rom_1_data[3:0]));  // open: dp

  // Notes on the sheet:
  //   contents of rom_1 (hex, n*v repeats v):
  //   0 1 2 3 4 5 6 7 8 9 10 11 12 13 14 15 16 17 18 19 20 21 22 23 24 25 26 27 28 29 30 31 32 33 34 35 36
  //   37 38 39 40 41 42 43 44 45 46 47 48 49 50 51 52 53 54 55 56 57 58 59 60 61 62 63 64 65 66 67 68 69
  //   70 71 72 73 74 75 76 77 78 79 80 81 82 83 84 85 86 87 88 89 90 91 92 93 94 95 96 97 98 99 100 101
  //   102 103 104 105 106 107 108 109 110 111 112 113 114 115 116 117 118 119 120 121 122 123 124 125 126
  //   127 128 129 130 131 132 133 134 135 136 137 138 139 140 141 142 143 144 145 146 147 148 149 150 151
  //   152 153 154 155 156 157 158 159 160 161 162 163 164 165 166 167 168 169 170 171 172 173 174 175 176
  //   177 178 179 180 181 182 183 184 185 186 187 188 189 190 191 192 193 194 195 196 197 198 199 200 201
  //   202 203 204 205 206 207 208 209 210 211 212 213 214 215 216 217 218 219 220 221 222 223 224 225 226
  //   227 228 229 230 231 232 233 234 235 236 237 238 239 240 241 242 243 244 245 246 247 248 249 250 251
  //   252 253 254 255 256 257 258 259 260 261 262 263 264 265 266 267 268 269 270 271 272 273 274 275 276
  //   277 278 279 280 281 282 283 284 285 286 287 288 289 290 291 292 293 294 295 296 297 298 299 300 301
  //   302 303 304 305 306 307 308 309 310 311 312 313 314 315 316 317 318 319 320 321 322 323 324 325 326
  //   327 328 329 330 331 332 333 334 335 336 337 338 339 340 341 342 343 344 345 346 347 348 349 350 351
  //   352 353 354 355 356 357 358 359 360 361 362 363 364 365 366 367 368 369 370 371 372 373 374 375 376
  //   377 378 379 380 381 382 383 384 385 386 387 388 389 390 391 392 393 394 395 396 397 398 399 400 401
  //   402 403 404 405 406 407 408 409 410 411 412 413 414 415 416 417 418 419 420 421 422 423 424 425 426
  //   427 428 429 430 431 432 433 434 435 436 437 438 439 440 441 442 443 444 445 446 447 448 449 450 451
  //   452 453 454 455 456 457 458 459 460 461 462 463 464 465 466 467 468 469 470 471 472 473 474 475 476
  //   477 478 479 480 481 482 483 484 485 486 487 488 489 490 491 492 493 494 495 496 497 498 499 500 501
  //   502 503 504 505 506 507 508 509 510 511 512 513 514 515 516 517 518 519 520 521 522 523 524 525 526
  //   527 528 529 530 531 532 533 534 535 536 537 538 539 540 541 542 543 544 545 546 547 548 549 550 551
  //   552 553 554 555 556 557 558 559 560 561 562 563 564 565 566 567 568 569 570 571 572 573 574 575 576
  //   577 578 579 580 581 582 583 584 585 586 587 588 589 590 591 592 593 594 595 596 597 598 599 600 601
  //   602 603 604 605 606 607 608 609 610 611 612 613 614 615 616 617 618 619 620 621 622 623 624 625 626
  //   627 628 629 630 631 632 633 634 635 636 637 638 639 640 641 642 643 644 645 646 647 648 649 650 651
  //   652 653 654 655 656 657 658 659 660 661 662 663 664 665 666 667 668 669 670 671 672 673 674 675 676
  //   677 678 679 680 681 682 683 684 685 686 687 688 689 690 691 692 693 694 695 696 697 698 699 700 701
  //   702 703 704 705 706 707 708 709 710 711 712 713 714 715 716 717 718 719 720 721 722 723 724 725 726
  //   727 728 729 730 731 732 733 734 735 736 737 738 739 740 741 742 743 744 745 746 747 748 749 750 751
  //   752 753 754 755 756 757 758 759 760 761 762 763 764 765 766 767 768 769 770 771 772 773 774 775 776
  //   777 778 779 780 781 782 783 784 785 786 787 788 789 790 791 792 793 794 795 796 797 798 799 800 801
  //   802 803 804 805 806 807 808 809 810 811 812 813 814 815 816 817 818 819 820 821 822 823 824 825 826
  //   827 828 829 830 831 832 833 834 835 836 837 838 839 840 841 842 843 844 845 846 847 848 849 850 851
  //   852 853 854 855 856 857 858 859 860 861 862 863 864 865 866 867 868 869 870 871 872 873 874 875 876
  //   877 878 879 880 881 882 883 884 885 886 887 888 889 890 891 892 893 894 895 896 897 898 899 900 901
  //   902 903 904 905 906 907 908 909 910 911 912 913 914 915 916 917 918 919 920 921 922 923 924 925 926
  //   927 928 929 930 931 932 933 934 935 936 937 938 939 940 941 942 943 944 945 946 947 948 949 950 951
  //   952 953 954 955 956 957 958 959 960 961 962 963 964 965 966 967 968 969 970 971 972 973 974 975 976
  //   977 978 979 980 981 982 983 984 985 986 987 988 989 990 991 992 993 994 995 996 997 998 999 1000
  //   1001 1002 1003 1004 1005 1006 1007 1008 1009 1010 1011 1012 1013 1014 1015 1016 1017 1018 1019 1020
  //   1021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
endmodule

module ClockController (
  input  RawCLK,
  input  Reset,
  output InstrLoad,
  output InstrExec,
  output InstrSave
);

  wire [1:0] counter_1_q;

  Counter #(.max('h3), .width(2)) counter_1 (
    .Q(counter_1_q), .clk(RawCLK), .clr(Reset));  // open: load, D, count, carry, up
  Decoder #(.select(2)) decoder_1 (
    .out0(InstrLoad), .out1(InstrExec), .out3(InstrSave), .sel(counter_1_q));  // open: out2, en
endmodule

module VGAController (
  input  EXT0_EN,
  input  [15:0] EXT0_A0,
  input  [15:0] EXT0_A1,
  input  EXT0_CLK,
  output [7:0] PixX,
  output [7:0] PixY,
  output [23:0] RGB,
  output CLK_Out
);


  assign CLK_Out = EXT0_CLK;
  assign PixX = EXT0_A0[7:0];
  assign PixY = EXT0_A0[15:8];
  assign RGB = {EXT0_A1[11:8], 4'b0000, EXT0_A1[7:4], 4'b0000, EXT0_A1[3:0], 4'b0000};
endmodule
